// Logisim project BOB-2200.circ as structural Verilog: 5 circuits, main circuit BOB-2200
module BOB_2200 (
);

  wire ALUHi, ALULo, ChkCmp, clk, CmpOut, comparsion_logic_1_output, CondType, DrALU, DrCmp, DrMEM, DrOFF,
       DrPC, DrREG, LdA, LdB, LdCmp, LdIR, LdMAR, LdPC, OPTest, RegSelHi, RegSelLo, WrMEM, WrREG;
  wire [3:0] regno;
  wire [31:0] A, alu_1_out, B, bit_extender_1_out, bit_extender_2_out, controlled_buffer_1_out, IR, MAR_q,
       PC_q, ram_1_data, registers_dout;

  control_unit Control_Unit (
    .CondType(CondType), .DrCmp(DrCmp), .ChkCmp(ChkCmp), .OPTest(OPTest), .ALUHi(ALUHi), .ALULo(ALULo),
    .RegSelHi(RegSelHi), .RegSelLo(RegSelLo), .WrMEM(WrMEM), .WrREG(WrREG), .LdCmp(LdCmp), .LdB(LdB),
    .LdA(LdA), .LdMAR(LdMAR), .LdIR(LdIR), .LdPC(LdPC), .DrOFF(DrOFF), .DrPC(DrPC), .DrALU(DrALU),
    .DrMEM(DrMEM), .DrREG(DrREG), .clk(clk), .OP(IR[31:28]), .CmpOut(CmpOut));
  // Probe on CondType
  // Probe on DrCmp
  // Probe on ChkCmp
  Register #(.width(32)) PC (.D(controlled_buffer_1_out), .en(LdPC), .Q(PC_q), .clk(clk));  // open: clr
  assign controlled_buffer_1_out = DrPC ? PC_q : 32'bz;  // Controlled_Buffer controlled_buffer_1
  Comparsion_Logic comparsion_logic_1 (
    .condType(CondType), .Input(controlled_buffer_1_out), .Output(comparsion_logic_1_output));
  // Probe on OPTest
  // Probe on ALUHi
  // Probe on ALULo
  Register #(.width(32)) u_A (.D(controlled_buffer_1_out), .en(LdA), .Q(A), .clk(clk));  // open: clr
  // Probe on controlled_buffer_1_out
  Register #(.width(1)) register_1 (.D(comparsion_logic_1_output), .en(LdCmp), .Q(CmpOut), .clk(clk));  // open: clr
  // Probe on RegSelHi
  // Probe on RegSelLo
  // Probe on WrMEM
  ALU alu_1 (.func({ALUHi, ALULo}), .A(A), .B(B), .out(alu_1_out));
  // Probe on {ALUHi, ALULo}
  assign controlled_buffer_1_out = DrALU ? alu_1_out : 32'bz;  // Controlled_Buffer controlled_buffer_2
  assign controlled_buffer_1_out = DrCmp ? bit_extender_1_out : 32'bz;  // Controlled_Buffer controlled_buffer_3
  assign bit_extender_1_out = {{31{1'b0}}, CmpOut};  // Bit_Extender bit_extender_1
  // Probe on CmpOut
  // Probe on WrREG
  // Probe on LdCmp
  // Probe on LdB
  Register #(.width(32)) u_B (.D(controlled_buffer_1_out), .en(LdB), .Q(B), .clk(clk));  // open: clr
  // Probe on controlled_buffer_1_out
  Registers registers (.WrREG(WrREG), .regno(regno), .Din(controlled_buffer_1_out), .clk(clk), .Dout(registers_dout));
  // Probe on LdA
  // Probe on LdMAR
  // Probe on LdIR
  assign controlled_buffer_1_out = DrREG ? registers_dout : 32'bz;  // Controlled_Buffer controlled_buffer_4
  Clock clock_1 (.out(clk));
  // Probe on LdPC
  // Probe on DrOFF
  // Probe on DrPC
  Register #(.width(32)) MAR (.D(controlled_buffer_1_out), .en(LdMAR), .Q(MAR_q), .clk(clk));  // open: clr
  // Probe on DrALU
  // Probe on DrMEM
  // Probe on DrREG
  RAM #(.addrWidth(24), .dataWidth(32), .bus("separate")) ram_1 (
    .addr(MAR_q[23:0]), .din(controlled_buffer_1_out), .data(ram_1_data), .str(WrMEM), .clk(clk));  // open: sel, ld, clr
  assign controlled_buffer_1_out = DrMEM ? ram_1_data : 32'bz;  // Controlled_Buffer controlled_buffer_5
  Multiplexer #(.select(2), .width(4), .disabled(0), .enable("false")) multiplexer_1 (
    .in0(IR[3:0]), .in1(IR[23:20]), .in2(IR[27:24]), .in3(IR[31:28]), .out(regno), .sel({RegSelHi, RegSelLo}));
  Register #(.width(32)) u_IR (.D(controlled_buffer_1_out), .en(LdIR), .Q(IR), .clk(clk));  // open: clr
  assign bit_extender_2_out = {{12{IR[19]}}, IR[19:0]};  // Bit_Extender bit_extender_2
  assign controlled_buffer_1_out = DrOFF ? bit_extender_2_out : 32'bz;  // Controlled_Buffer controlled_buffer_6

  // Other names for the same wires on the sheet: func[1:0] = {ALUHi, ALULo}; Offset[19:0] = IR[19:0];
  //   OP[3:0] = IR[31:28]; Rx[3:0] = IR[27:24]; Ry[3:0] = IR[23:20]; Rz[3:0] = IR[3:0]
endmodule

module ALU (
  input  [31:0] A,
  input  [31:0] B,
  input  [1:0] func,
  output [31:0] out
);

  wire [31:0] adder_1_out, adder_2_out, nand_1_out, subtractor_1_out;

  Adder #(.width(32)) adder_1 (.a(B), .b(A), .out(adder_1_out), .cin(1'b0));  // open: cout
  Subtractor #(.width(32)) subtractor_1 (.a(A), .b(B), .out(subtractor_1_out), .bin(1'b0));  // open: bout
  assign nand_1_out = ~(B & A);  // NAND_Gate nand_1, 32 bits wide
  Adder #(.width(32)) adder_2 (.a(32'h1), .b(A), .out(adder_2_out), .cin(1'b0));  // open: cout
  Multiplexer #(.select(2), .width(32), .disabled(0), .enable("false")) multiplexer_1 (
    .in0(adder_1_out), .in1(subtractor_1_out), .in2(nand_1_out), .in3(adder_2_out), .out(out), .sel(func));
endmodule

module Registers (
  input  [31:0] Din,
  input  WrREG,
  input  [3:0] regno,
  input  clk,
  output [31:0] Dout
);

  wire and_1_out, and_2_out, and_3_out, and_4_out, and_5_out, and_6_out, and_7_out, and_8_out, and_9_out,
       and_10_out, and_11_out, and_12_out, and_13_out, and_14_out, and_15_out, and_16_out, D0, D1, D2, D3,
       D4, D5, D6, D7, D8, D9, D10, D11, D12, D13, D14, D15;
  wire [31:0] Reg0, Reg1, Reg2, Reg3, Reg4, Reg5, Reg6, Reg7, Reg8, Reg9, Reg10, Reg11, Reg12, Reg13, Reg14,
       Reg15;

  Register #(.width(32)) zero (.D(Din), .en(and_1_out), .Q(Reg0), .clk(clk));  // open: clr
  and and_1 (and_1_out, WrREG, D0);
  Register #(.width(32)) at (.D(Din), .en(and_2_out), .Q(Reg1), .clk(clk));  // open: clr
  and and_2 (and_2_out, WrREG, D1);
  Register #(.width(32)) v0 (.D(Din), .en(and_3_out), .Q(Reg2), .clk(clk));  // open: clr
  and and_3 (and_3_out, WrREG, D2);
  Register #(.width(32)) a0 (.D(Din), .en(and_4_out), .Q(Reg3), .clk(clk));  // open: clr
  and and_4 (and_4_out, WrREG, D3);
  Register #(.width(32)) a1 (.D(Din), .en(and_5_out), .Q(Reg4), .clk(clk));  // open: clr
  and and_5 (and_5_out, WrREG, D4);
  Register #(.width(32)) a2 (.D(Din), .en(and_6_out), .Q(Reg5), .clk(clk));  // open: clr
  and and_6 (and_6_out, WrREG, D5);
  Register #(.width(32)) t0 (.D(Din), .en(and_7_out), .Q(Reg6), .clk(clk));  // open: clr
  and and_7 (and_7_out, WrREG, D6);
  Register #(.width(32)) t1 (.D(Din), .en(and_8_out), .Q(Reg7), .clk(clk));  // open: clr
  and and_8 (and_8_out, WrREG, D7);
  Multiplexer #(.select(4), .width(32), .disabled(0), .enable("false")) multiplexer_1 (
    .in0({32{1'b0}}), .in1(Reg1), .in2(Reg2), .in3(Reg3), .in4(Reg4), .in5(Reg5), .in6(Reg6), .in7(Reg7),
    .in8(Reg8), .in9(Reg9), .in10(Reg10), .in11(Reg11), .in12(Reg12), .in13(Reg13), .in14(Reg14),
    .in15(Reg15), .out(Dout), .sel(regno));
  Decoder #(.select(4), .enable("false")) decoder_1 (
    .out0(D0), .out1(D1), .out2(D2), .out3(D3), .out4(D4), .out5(D5), .out6(D6), .out7(D7), .out8(D8),
    .out9(D9), .out10(D10), .out11(D11), .out12(D12), .out13(D13), .out14(D14), .out15(D15), .sel(regno));
  Register #(.width(32)) t2 (.D(Din), .en(and_9_out), .Q(Reg8), .clk(clk));  // open: clr
  and and_9 (and_9_out, WrREG, D8);
  Register #(.width(32)) s0 (.D(Din), .en(and_10_out), .Q(Reg9), .clk(clk));  // open: clr
  and and_10 (and_10_out, WrREG, D9);
  and and_11 (and_11_out, WrREG, D10);
  and and_12 (and_12_out, WrREG, D11);
  Register #(.width(32)) s1 (.D(Din), .en(and_11_out), .Q(Reg10), .clk(clk));  // open: clr
  Register #(.width(32)) s2 (.D(Din), .en(and_12_out), .Q(Reg11), .clk(clk));  // open: clr
  Register #(.width(32)) k0 (.D(Din), .en(and_13_out), .Q(Reg12), .clk(clk));  // open: clr
  and and_13 (and_13_out, WrREG, D12);
  Register #(.width(32)) sp (.D(Din), .en(and_14_out), .Q(Reg13), .clk(clk));  // open: clr
  and and_14 (and_14_out, WrREG, D13);
  and and_15 (and_15_out, WrREG, D14);
  and and_16 (and_16_out, WrREG, D15);
  Register #(.width(32)) fp (.D(Din), .en(and_15_out), .Q(Reg14), .clk(clk));  // open: clr
  Register #(.width(32)) ra (.D(Din), .en(and_16_out), .Q(Reg15), .clk(clk));  // open: clr

  // Other names for the same wires on the sheet: input[31:0] = Din; regsel[3:0] = regno; wrmem = WrREG
endmodule

module Comparsion_Logic (
  input  [31:0] Input,
  input  condType,
  output Output
);

  wire comparator_1_gt, comparator_2_eq;

  Comparator #(.width(32)) comparator_1 (.a(Input), .b({32{1'b0}}), .gt(comparator_1_gt));  // open: eq, lt
  Comparator #(.width(32)) comparator_2 (.a(Input), .b({32{1'b0}}), .eq(comparator_2_eq));  // open: gt, lt
  // Probe on condType
  Multiplexer #(.disabled(0), .enable("false")) multiplexer_1 (
    .in0(comparator_1_gt), .in1(comparator_2_eq), .out(Output), .sel(condType));
  // Probe on Output
endmodule

module control_unit (
  input  clk,
  input  [3:0] OP,
  input  CmpOut,
  output CondType,
  output DrCmp,
  output ChkCmp,
  output OPTest,
  output ALUHi,
  output ALULo,
  output RegSelHi,
  output RegSelLo,
  output WrMEM,
  output WrREG,
  output LdCmp,
  output LdB,
  output LdA,
  output LdMAR,
  output LdIR,
  output LdPC,
  output DrOFF,
  output DrPC,
  output DrALU,
  output DrMEM,
  output DrREG
);

  wire NS_0, NS_1, NS_2, NS_3, NS_4, NS_5;
  wire [5:0] multiplexer_1_out, register_1_q, rom_2_data, rom_3_data;

  Register #(.width(6)) register_1 (.D(multiplexer_1_out), .en(1'b1), .Q(register_1_q), .clk(clk));  // open: clr
  ROM #(.addrWidth(6), .dataWidth(27)) rom_1 (
    .addr(register_1_q),
    .data({CondType, DrCmp, ChkCmp, OPTest, ALUHi, ALULo, RegSelHi, RegSelLo, WrMEM, WrREG, LdCmp, LdB, LdA, LdMAR, LdIR, LdPC, DrOFF, DrPC, DrALU, DrMEM, DrREG, NS_5, NS_4, NS_3, NS_2, NS_1, NS_0}),
    .sel(1'b1));
  Multiplexer #(.select(2), .width(6), .disabled(0), .enable("false")) multiplexer_1 (
    .in0({NS_5, NS_4, NS_3, NS_2, NS_1, NS_0}), .in1(rom_2_data), .in2(rom_3_data), .out(multiplexer_1_out),
    .sel({ChkCmp, OPTest}));  // open: in3
  ROM #(.addrWidth(4), .dataWidth(6)) rom_2 (.addr(OP), .data(rom_2_data), .sel(1'b1));
  ROM #(.addrWidth(2), .dataWidth(6)) rom_3 (.addr({1'b0, CmpOut}), .data(rom_3_data), .sel(1'b1));

  // Notes on the sheet:
  //   contents of rom_1 (hex, n*v repeats v):
  //   6201 1082 e00900 4044 88045 120100 84047 108048 420100 8404a 840b 120100 8404d 840e 210f 120080
  //   84051 8412 2113 140040 104055 88056 4210117 1000000 8419 421a 900 12021c 80840 1d 405f 88060 210121
  //   2120000 4223 8424 120100
  //   contents of rom_2 (hex, n*v repeats v):
  //   3 6 9 c 10 14 1b 1d 1e 22
  //   contents of rom_3 (hex, n*v repeats v):
  //   18
endmodule
