// Logisim project BOB-2200a.circ as structural Verilog: 6 circuits, main circuit Timer Device
module Timer_Device (
  input  Clock,
  input  IntAck_In,
  input  [31:0] Limit,
  input  [31:0] ID,
  output Int,
  output [31:0] Data,
  output IntAck_Out
);

  wire and_3_out, button_1_out, comparator_1_eq, comparator_1_gt, IntAck, IntRaise, not_1_out, or_1_out,
       PushID;
  wire [31:0] Timer_q;

  assign IntAck = IntAck_In ? 1'b1 : 1'bz;  // Controlled_Buffer controlled_buffer_1
  Pull_Resistor pull_resistor_1 (.node(IntAck));
  and and_1 (PushID, IntRaise, IntAck);
  assign Int = IntRaise ? 1'b1 : 1'bz;  // Controlled_Buffer controlled_buffer_2
  and and_2 (IntAck_Out, IntAck, ~IntRaise);  // AND_Gate
  not not_1 (not_1_out, IntAck);
  Counter #(.width(32), .max('hffffffff), .ongoal("stay")) Timer (
    .load(IntAck), .D({32{1'b0}}), .count(not_1_out), .Q(Timer_q), .clk(Clock), .clr(button_1_out));  // open: carry
  Button button_1 (.out(button_1_out));
  assign Data = PushID ? ID : 32'bz;  // Controlled_Buffer controlled_buffer_3
  Comparator #(.width(32), .mode("unsigned")) comparator_1 (
    .a(Timer_q), .b(Limit), .gt(comparator_1_gt), .eq(comparator_1_eq));  // open: lt
  or or_1 (or_1_out, comparator_1_gt, comparator_1_eq);
  and and_3 (and_3_out, or_1_out, ~IntAck);  // AND_Gate
  D_Flip_Flop d_ff_1 (.clk(Clock), .D(and_3_out), .Q(IntRaise));  // open: Qn, preset, en, reset

  // Other names for the same wires on the sheet: DeviceID[31:0] = ID

  // Notes on the sheet:
  //   Clear Button
endmodule

module registers_file (
  input  [31:0] Din,
  input  clk,
  input  WrREG,
  input  [3:0] regno,
  output [31:0] Dout
);

  wire and_1_out, and_2_out, and_3_out, and_4_out, and_5_out, and_6_out, and_7_out, and_8_out, and_9_out,
       and_10_out, and_11_out, and_12_out, and_13_out, and_14_out, and_15_out, and_16_out, regin0, regin1,
       regin2, regin3, regin4, regin5, regin6, regin7, regin8, regin9, regin10, regin11, regin12, regin13,
       regin14, regin15;
  wire [31:0] reg0, reg1, reg2, reg3, reg4, reg5, reg6, reg7, reg8, reg9, reg10, reg11, reg12, reg13, reg14,
       reg15;

  and and_1 (and_1_out, WrREG, regin0);
  and and_2 (and_2_out, WrREG, regin4);
  and and_3 (and_3_out, WrREG, regin8);
  and and_4 (and_4_out, WrREG, regin12);
  Register #(.width(32)) zero (.D(Din), .en(and_1_out), .Q(reg0), .clk(clk));  // open: clr
  Register #(.width(32)) a1 (.D(Din), .en(and_2_out), .Q(reg4), .clk(clk));  // open: clr
  Register #(.width(32)) t2 (.D(Din), .en(and_3_out), .Q(reg8), .clk(clk));  // open: clr
  Register #(.width(32)) k0 (.D(Din), .en(and_4_out), .Q(reg12), .clk(clk));  // open: clr
  and and_5 (and_5_out, WrREG, regin1);
  and and_6 (and_6_out, WrREG, regin5);
  and and_7 (and_7_out, WrREG, regin9);
  and and_8 (and_8_out, WrREG, regin13);
  Register #(.width(32)) at (.D(Din), .en(and_5_out), .Q(reg1), .clk(clk));  // open: clr
  Register #(.width(32)) a2 (.D(Din), .en(and_6_out), .Q(reg5), .clk(clk));  // open: clr
  Register #(.width(32)) s0 (.D(Din), .en(and_7_out), .Q(reg9), .clk(clk));  // open: clr
  Register #(.width(32)) sp (.D(Din), .en(and_8_out), .Q(reg13), .clk(clk));  // open: clr
  Multiplexer #(.select(4), .width(32), .disabled(0), .enable("false")) multiplexer_1 (
    .in0({32{1'b0}}), .in1(reg1), .in2(reg2), .in3(reg3), .in4(reg4), .in5(reg5), .in6(reg6), .in7(reg7),
    .in8(reg8), .in9(reg9), .in10(reg10), .in11(reg11), .in12(reg12), .in13(reg13), .in14(reg14),
    .in15(reg15), .out(Dout), .sel(regno));
  and and_9 (and_9_out, WrREG, regin2);
  and and_10 (and_10_out, WrREG, regin6);
  and and_11 (and_11_out, WrREG, regin10);
  and and_12 (and_12_out, WrREG, regin14);
  Demultiplexer #(.select(4), .disabled(0), .enable("false")) demultiplexer_1 (
    .out0(regin0), .out1(regin1), .out2(regin2), .out3(regin3), .out4(regin4), .out5(regin5), .out6(regin6),
    .out7(regin7), .out8(regin8), .out9(regin9), .out10(regin10), .out11(regin11), .out12(regin12),
    .out13(regin13), .out14(regin14), .out15(regin15), .sel(regno));  // open: in
  Register #(.width(32)) v0 (.D(Din), .en(and_9_out), .Q(reg2), .clk(clk));  // open: clr
  Register #(.width(32)) t0 (.D(Din), .en(and_10_out), .Q(reg6), .clk(clk));  // open: clr
  Register #(.width(32)) s1 (.D(Din), .en(and_11_out), .Q(reg10), .clk(clk));  // open: clr
  Register #(.width(32)) fp (.D(Din), .en(and_12_out), .Q(reg14), .clk(clk));  // open: clr
  and and_13 (and_13_out, WrREG, regin3);
  and and_14 (and_14_out, WrREG, regin7);
  and and_15 (and_15_out, WrREG, regin11);
  and and_16 (and_16_out, WrREG, regin15);
  Register #(.width(32)) a0 (.D(Din), .en(and_13_out), .Q(reg3), .clk(clk));  // open: clr
  Register #(.width(32)) t1 (.D(Din), .en(and_14_out), .Q(reg7), .clk(clk));  // open: clr
  Register #(.width(32)) s2 (.D(Din), .en(and_15_out), .Q(reg11), .clk(clk));  // open: clr
  Register #(.width(32)) ra (.D(Din), .en(and_16_out), .Q(reg15), .clk(clk));  // open: clr

  // Other names for the same wires on the sheet: input[31:0] = Din
endmodule

module ALU (
  input  [31:0] A,
  input  [31:0] B,
  input  [1:0] func,
  output [31:0] out
);

  wire [31:0] adder_1_out, adder_2_out, nand_1_out, subtractor_1_out;

  Adder #(.width(32)) adder_1 (.a(A), .b(B), .out(adder_1_out), .cin(1'b0));  // open: cout
  Subtractor #(.width(32)) subtractor_1 (.a(A), .b(B), .out(subtractor_1_out), .bin(1'b0));  // open: bout
  Adder #(.width(32)) adder_2 (.a(32'h1), .b(A), .out(adder_2_out), .cin(1'b0));  // open: cout
  assign nand_1_out = ~(A & B);  // NAND_Gate nand_1, 32 bits wide
  Multiplexer #(.select(2), .width(32), .disabled(0), .enable("false")) multiplexer_1 (
    .in0(adder_1_out), .in1(subtractor_1_out), .in2(nand_1_out), .in3(adder_2_out), .out(out), .sel(func));
endmodule

module control_unit (
  input  clk,
  input  [3:0] IR_31_28,
  input  CmpOut,
  input  OnInt,
  output DrIO,
  output IntAck,
  output EnInt,
  output LdEnInt,
  output CondType,
  output DrCmp,
  output ChkCmp,
  output OPTest,
  output ALUHi,
  output ALULo,
  output RegSelHi,
  output RegSelLo,
  output WrMEM,
  output WrREG,
  output LdCmp,
  output LdB,
  output LdA,
  output LdMAR,
  output LdIR,
  output LdPC,
  output DrOFF,
  output DrPC,
  output DrALU,
  output DrMEM,
  output DrREG
);

  wire IE_register_q, NS_0, NS_1, NS_2, NS_3, NS_4, NS_5;
  wire [0:0] and_1_out;
  wire [5:0] multiplexer_1_out, register_1_q, rom_1_data, rom_3_data, rom_4_data;

  Register #(.width(1)) IE_register (.D(EnInt), .en(LdEnInt), .Q(IE_register_q), .clk(clk));  // open: clr
  Register #(.width(6)) register_1 (.D(multiplexer_1_out), .en(1'b1), .Q(register_1_q), .clk(clk));  // open: clr
  and and_1 (and_1_out[0], IE_register_q, OnInt);
  ROM #(.addrWidth(2), .dataWidth(6)) rom_1 (.addr({1'b0, and_1_out[0]}), .data(rom_1_data), .sel(1'b1));
  ROM #(.addrWidth(6), .dataWidth(31)) rom_2 (
    .addr(register_1_q),
    .data({DrIO, IntAck, EnInt, LdEnInt, CondType, DrCmp, ChkCmp, OPTest, ALUHi, ALULo, RegSelHi, RegSelLo, WrMEM, WrREG, LdCmp, LdB, LdA, LdMAR, LdIR, LdPC, DrOFF, DrPC, DrALU, DrMEM, DrREG, NS_5, NS_4, NS_3, NS_2, NS_1, NS_0}),
    .sel(1'b1));
  Multiplexer #(.select(2), .width(6), .disabled(0), .enable("false")) multiplexer_1 (
    .in0({NS_5, NS_4, NS_3, NS_2, NS_1, NS_0}), .in1(rom_4_data), .in2(rom_3_data), .in3(rom_1_data),
    .out(multiplexer_1_out), .sel({ChkCmp, OPTest}));
  // Probe on NS_5
  ROM #(.addrWidth(2), .dataWidth(6)) rom_3 (.addr({1'b0, CmpOut}), .data(rom_3_data), .sel(1'b1));
  // Probe on NS_3
  // Probe on NS_4
  // Probe on NS_1
  // Probe on NS_2
  ROM #(.addrWidth(4), .dataWidth(6)) rom_4 (.addr(IR_31_28), .data(rom_4_data), .sel(1'b1));
  // Probe on NS_0

  // Notes on the sheet:
  //   contents of rom_1 (hex, n*v repeats v):
  //   1 29
  //   contents of rom_2 (hex, n*v repeats v):
  //   1800001 6202 1083 e00900 4045 88046 120100 84048 108049 420100 8404b 840c 120100 8404e 840f 2110
  //   120080 84052 8413 2114 140040 104056 88057 4210118 1000000 841a 421b 900 12021d 80840 1e 4060 88061
  //   210122 2120000 4224 8425 120100 18000000 8000000 18180840 1a022a 800002b 6000202c 880
  //   contents of rom_3 (hex, n*v repeats v):
  //   19
  //   contents of rom_4 (hex, n*v repeats v):
  //   4 7 a d 11 15 1c 1e 1f 23 26 27 28
endmodule

module BOB_2200a (
);

  wire ALUHi, ALULo, ChkCmp, clk, CmpOut, comparator_1_gt, comparsion_logic_1_output, CondType, DrALU, DrCmp,
       DrIO, DrMEM, DrOFF, DrPC, DrREG, EnInt, IntAck, LdA, LdB, LdCmp, LdEnInt, LdIR, LdMAR, LdPC, OnInt,
       OPTest, RegSelHi, RegSelLo, WrMEM, WrREG;
  wire [3:0] regno;
  wire [31:0] A, alu_1_out, B, bit_extender_1_out, bit_extender_2_out, controlled_buffer_1_out, IR, MAR_q,
       multiplexer_1_out, PC_q, ram_1_data, registers_file_1_dout, timer_device_1_data;

  Clock clock_1 (.out(clk));
  control_unit control_unit (
    .IR_31_28(IR[31:28]), .CmpOut(CmpOut), .OnInt(OnInt), .clk(clk), .DrIO(DrIO), .IntAck(IntAck),
    .EnInt(EnInt), .LdEnInt(LdEnInt), .CondType(CondType), .DrCmp(DrCmp), .ChkCmp(ChkCmp), .OPTest(OPTest),
    .ALUHi(ALUHi), .ALULo(ALULo), .RegSelHi(RegSelHi), .RegSelLo(RegSelLo), .WrMEM(WrMEM), .WrREG(WrREG),
    .LdCmp(LdCmp), .LdB(LdB), .LdA(LdA), .LdMAR(LdMAR), .LdIR(LdIR), .LdPC(LdPC), .DrOFF(DrOFF), .DrPC(DrPC),
    .DrALU(DrALU), .DrMEM(DrMEM), .DrREG(DrREG));
  Register #(.width(32)) PC (.D(controlled_buffer_1_out), .en(LdPC), .Q(PC_q), .clk(clk));  // open: clr
  Comparator #(.width(32)) comparator_1 (.a(PC_q), .b(32'h10), .gt(comparator_1_gt));  // open: eq, lt
  // Probe on multiplexer_1_out
  Multiplexer #(.width(32), .disabled(0), .enable("false")) multiplexer_1 (
    .in0(32'h10), .in1(PC_q), .out(multiplexer_1_out), .sel(comparator_1_gt));
  assign controlled_buffer_1_out = DrPC ? multiplexer_1_out : 32'bz;  // Controlled_Buffer controlled_buffer_1
  Comparsion_Logic comparsion_logic_1 (
    .condType(CondType), .\input (controlled_buffer_1_out), .Output(comparsion_logic_1_output));
  Register #(.width(32)) u_A (.D(controlled_buffer_1_out), .en(LdA), .Q(A), .clk(clk));  // open: clr
  ALU alu_1 (.func({ALUHi, ALULo}), .A(A), .B(B), .out(alu_1_out));
  assign controlled_buffer_1_out = DrALU ? alu_1_out : 32'bz;  // Controlled_Buffer controlled_buffer_2
  Register #(.width(1)) register_1 (.D(comparsion_logic_1_output), .en(LdCmp), .Q(CmpOut), .clk(clk));  // open: clr
  Pull_Resistor pull_resistor_1 (.node(OnInt));
  Register #(.width(32)) u_B (.D(controlled_buffer_1_out), .en(LdB), .Q(B), .clk(clk));  // open: clr
  assign controlled_buffer_1_out = DrCmp ? bit_extender_1_out : 32'bz;  // Controlled_Buffer controlled_buffer_3
  assign bit_extender_1_out = {{31{1'b0}}, CmpOut};  // Bit_Extender bit_extender_1
  registers_file registers_file_1 (
    .WrREG(WrREG), .regno(regno), .Din(controlled_buffer_1_out), .clk(clk), .Dout(registers_file_1_dout));
  assign controlled_buffer_1_out = DrREG ? registers_file_1_dout : 32'bz;  // Controlled_Buffer controlled_buffer_4
  Timer_Device timer_device_1 (
    .Clock(clk), .Data(timer_device_1_data), .IntAck_In(IntAck), .Int(OnInt), .Limit(32'h3e8), .ID(32'h1));  // open: IntAck_Out
  Register #(.width(32)) MAR (.D(controlled_buffer_1_out), .en(LdMAR), .Q(MAR_q), .clk(clk));  // open: clr
  assign controlled_buffer_1_out = DrIO ? timer_device_1_data : 32'bz;  // Controlled_Buffer controlled_buffer_5
  RAM #(.addrWidth(24), .dataWidth(32), .bus("separate")) ram_1 (
    .addr(MAR_q[23:0]), .din(controlled_buffer_1_out), .data(ram_1_data), .str(WrMEM), .clk(clk));  // open: sel, ld, clr
  assign controlled_buffer_1_out = DrMEM ? ram_1_data : 32'bz;  // Controlled_Buffer controlled_buffer_6
  Register #(.width(32)) u_IR (.D(controlled_buffer_1_out), .en(LdIR), .Q(IR), .clk(clk));  // open: clr
  assign bit_extender_2_out = {{12{IR[19]}}, IR[19:0]};  // Bit_Extender bit_extender_2
  assign controlled_buffer_1_out = DrOFF ? bit_extender_2_out : 32'bz;  // Controlled_Buffer controlled_buffer_7
  Multiplexer #(.select(2), .width(4), .disabled(0), .enable("false")) multiplexer_2 (
    .in0(IR[3:0]), .in1(IR[23:20]), .in2(IR[27:24]), .in3(4'b1100), .out(regno), .sel({RegSelHi, RegSelLo}));

  // Other names for the same wires on the sheet: func[1:0] = {ALUHi, ALULo}; Offset[19:0] = IR[19:0];
  //   OP[3:0] = IR[31:28]; Rx[3:0] = IR[27:24]; Ry[3:0] = IR[23:20]; Rz[3:0] = IR[3:0]
endmodule

module Comparsion_Logic (
  input  [31:0] \input ,
  input  condType,
  output Output
);

  wire comparator_1_gt, comparator_2_eq;

  Comparator #(.width(32)) comparator_1 (.a(\input ), .b({32{1'b0}}), .gt(comparator_1_gt));  // open: eq, lt
  Multiplexer #(.disabled(0), .enable("false")) multiplexer_1 (
    .in0(comparator_1_gt), .in1(comparator_2_eq), .out(Output), .sel(condType));
  Comparator #(.width(32)) comparator_2 (.a(\input ), .b({32{1'b0}}), .eq(comparator_2_eq));  // open: gt, lt
endmodule
