// Logisim project BOB2200-pipeline(Sample).circ as structural Verilog: 7 circuits, main circuit main
module main (
  input  in_1
);

  wire and_1_out, and_2_out, and_3_out, BR_EN, BR_NT, CLK, CLR, comparator_1_eq, comparator_2_eq,
       comparator_3_eq, comparator_4_eq, comparator_6_eq, LdPC, not_1_out, not_2_out, not_3_out, not_4_out,
       or_1_out, or_2_out, PC_2_q, Stall, WrEN;
  wire [1:0] WBSel;
  wire [2:0] adder_3_out, PC_3_q;
  wire [3:0] multiplexer_5_out, op, regno, RX, RY, RZ, X, Y, Z;
  wire [19:4] ram_1_data;
  wire [31:0] adder_1_out, alu_1_out, BR, control_sig, control_sig2, control_sig3, Data,
       dual_ported_register_file_1_out1, dual_ported_register_file_1_out2, EX_MEM_out_12, EX_MEM_out_13,
       EX_MEM_pc_out, IDRR_EX_out_12, IF_IDRR_pc_out, imm, MEM_WB_out_11, MEM_WB_out_12, MEM_WB_out_15,
       MEM_WB_pc_out, multiplexer_1_out, multiplexer_2_out, multiplexer_3_out, Out1, PC, PC_1, ram_2_data,
       RX_val;
  wire [31:4] IF_IDRR_out_15;

  Adder #(.width(32)) adder_1 (.a(32'h1), .b(PC), .out(adder_1_out));  // open: cin, cout
  Register #(.width(32)) u_PC (.D(multiplexer_2_out), .en(LdPC), .Q(PC), .clk(CLK), .clr(CLR));
  ALU alu_1 (.FUNC(control_sig2[5:4]), .A(Out1), .B(multiplexer_1_out), .OUT(alu_1_out));
  Multiplexer #(.width(32), .disabled(0), .enable("false")) multiplexer_1 (
    .in0(IDRR_EX_out_12), .in1(imm), .out(multiplexer_1_out), .sel(control_sig2[6]));
  Adder #(.width(32)) adder_2 (.a(PC_1), .b(imm), .out(BR));  // open: cin, cout
  Multiplexer #(.select(2), .width(32), .disabled(0), .enable("false")) multiplexer_2 (
    .in0(adder_1_out), .in1(RX_val), .in2(BR), .out(multiplexer_2_out), .sel(control_sig2[1:0]));  // open: in3
  RAM #(.addrWidth(24), .dataWidth(32), .bus("separate")) ram_1 (
    .addr(PC[23:0]), .data({op, X, Y, ram_1_data, Z}), .ld(1'b1));  // open: din, str, sel, clk, clr
  and and_1 (and_1_out, comparator_1_eq, BR_EN);
  Comparator #(.width(32), .mode("unsigned")) comparator_1 (
    .a(alu_1_out), .b({32{1'b0}}), .gt(BR_NT), .eq(comparator_1_eq));  // open: lt
  Clock clock_1 (.out(CLK));
  Button button_1 (.out(CLR));
  Comparator #(.width(4), .mode("unsigned")) comparator_2 (.a(Z), .b(RX), .eq(comparator_2_eq));  // open: gt, lt
  Comparator #(.width(32), .mode("unsigned")) comparator_3 (
    .a(PC), .b({32{1'b0}}), .eq(comparator_3_eq));  // open: gt, lt
  not not_1 (not_1_out, comparator_3_eq);
  Comparator #(.width(4), .mode("unsigned")) comparator_4 (.a(Y), .b(RX), .eq(comparator_4_eq));  // open: gt, lt
  Multiplexer #(.width(32), .disabled(0), .enable("false")) multiplexer_3 (
    .in0(alu_1_out), .in1(BR), .out(multiplexer_3_out), .sel(and_1_out));
  and and_2 (and_2_out, comparator_2_eq, not_1_out);
  and and_3 (and_3_out, not_1_out, comparator_4_eq);
  IF_IDRR_Buffer IF_IDRR (
    .PC_In(adder_1_out), .in_6({op, X, Y, ram_1_data, Z}), .EN(in_1), .CLK(CLK), .CLR(CLR),
    .PC_Out(IF_IDRR_pc_out), .out_15({IF_IDRR_out_15[31:28], RX, RY, IF_IDRR_out_15[19:4], RZ}));  // open: in_2, in_3, in_4, in_5, out_11, out_12, out_13, out_14
  EX_MEM_Buffer EX_MEM (
    .PC_In(PC_1), .in_3(multiplexer_3_out), .in_4(RX_val),
    .in_6({control_sig2[31:8], BR_EN, control_sig2[6:0]}), .EN(in_1), .CLK(CLK), .CLR(CLR),
    .PC_Out(EX_MEM_pc_out), .out_12(EX_MEM_out_12), .out_13(EX_MEM_out_13), .out_15(control_sig3));  // open: in_2, in_5, out_11, out_14
  Multiplexer #(.width(4), .disabled(0), .enable("false")) multiplexer_4 (
    .in0(RX), .in1(RY), .out(regno), .sel(control_sig[11]));
  or or_1 (or_1_out, and_2_out, and_3_out);
  not not_2 (not_2_out, Stall);
  Register #(.width(1)) PC_2 (.D(or_1_out), .en(not_2_out), .Q(PC_2_q), .clk(or_1_out), .clr(Stall));
  Adder #(.width(3)) adder_3 (.a(3'b000), .b(3'b001), .out(adder_3_out));  // open: cin, cout
  Register #(.width(3)) PC_3 (.D(adder_3_out), .en(PC_2_q), .Q(PC_3_q), .clk(CLK), .clr(Stall));
  Multiplexer #(.width(4), .disabled(0), .enable("false")) multiplexer_5 (
    .in0(RZ), .in1(RX), .out(multiplexer_5_out), .sel(control_sig[2]));
  RAM #(.addrWidth(24), .dataWidth(32), .bus("separate")) ram_2 (
    .addr(EX_MEM_out_12[23:0]), .din(EX_MEM_out_13), .data(ram_2_data), .str(control_sig3[8]), .clk(CLK),
    .clr(CLR));  // open: sel, ld
  Comparator #(.width(3), .mode("unsigned")) comparator_5 (.a(PC_3_q), .b(3'b100), .eq(Stall));  // open: gt, lt
  ROM #(.addrWidth(4), .dataWidth(32)) rom_1 (.addr(IF_IDRR_out_15[31:28]), .data(control_sig));  // open: sel
  MEM_WB_Buffer MEM_WB (
    .PC_In(EX_MEM_pc_out), .in_2(EX_MEM_out_12), .in_3(ram_2_data), .in_6(control_sig3), .EN(in_1),
    .CLK(CLK), .CLR(CLR), .PC_Out(MEM_WB_pc_out), .out_11(MEM_WB_out_11), .out_12(MEM_WB_out_12),
    .out_15({MEM_WB_out_15[31:11], WBSel, MEM_WB_out_15[8:4], WrEN, control_sig[2], MEM_WB_out_15[1:0]}));  // open: in_4, in_5, out_13, out_14
  Dual_Ported_Register_File dual_ported_register_file_1 (
    .CLK(CLK), .WrREGNO(regno), .RdREGNO1(RY), .RdREGNO2(multiplexer_5_out), .INPUT(Data),
    .OUT1(dual_ported_register_file_1_out1), .OUT2(dual_ported_register_file_1_out2), .WrEN(WrEN));
  Comparator #(.width(4), .mode("unsigned")) comparator_6 (.a(op), .b(4'b0101), .eq(comparator_6_eq));  // open: gt, lt
  IDRR_EX_Buffer IDRR_EX (
    .PC_In(IF_IDRR_pc_out), .in_2(dual_ported_register_file_1_out1), .in_3(dual_ported_register_file_1_out2),
    .in_4(dual_ported_register_file_1_out2), .in_5({{12{1'b0}}, IF_IDRR_out_15[19:4], RZ}),
    .in_6(control_sig), .EN(in_1), .CLK(CLK), .CLR(CLR), .PC_Out(PC_1), .out_11(Out1),
    .out_12(IDRR_EX_out_12), .out_13(RX_val), .out_14(imm),
    .out_15({control_sig2[31:8], BR_EN, control_sig2[6:0]}));
  Multiplexer #(.select(2), .width(32), .disabled(0), .enable("false")) multiplexer_6 (
    .in0(MEM_WB_pc_out), .in1(MEM_WB_out_11), .in2(MEM_WB_out_12), .out(Data), .sel(WBSel));  // open: in3
  not not_3 (not_3_out, comparator_6_eq);
  or or_2 (or_2_out, not_3_out, BR_NT);
  and and_4 (LdPC, or_2_out, not_4_out);
  not not_4 (not_4_out, Stall);

  // Other names for the same wires on the sheet: Sig1[31:0] = control_sig;
  //   Sig2[31:0] = {control_sig2[31:8], BR_EN, control_sig2[6:0]}; Sig3[31:0] = control_sig3; brnt = BR_NT;
  //   DstReg = control_sig[2]; regY = control_sig[11]; ImmSel = control_sig2[6]; control_sig2[7] = BR_EN;
  //   WrMEM = control_sig3[8]; En = in_1; func[1:0] = control_sig2[5:4]; PCAddrSel[1:0] = control_sig2[1:0];
  //   StallOff = Stall

  // Notes on the sheet:
  //   opcode
  //   sign extended imme
  //   PC+1
  //   control signal
endmodule

module Dual_Ported_Register_File (
  input  CLK,
  input  WrEN,
  input  [3:0] WrREGNO,
  input  [3:0] RdREGNO1,
  input  [3:0] RdREGNO2,
  input  [31:0] INPUT,
  output [31:0] OUT1,
  output [31:0] OUT2
);

  wire En_a0, En_a1, En_a2, En_a3, En_a4, En_at, En_fp, En_k0, En_ra, En_s0, En_s1, En_s2, En_s3, En_sp,
       En_v0;
  wire [31:0] a0, a1, a2, a3, a4, at, fp, k0, ra, s0, s1, s2, s3, sp, v0, zero;

  Decoder #(.select(4), .disabled(0)) decoder_1 (
    .out1(En_at), .out2(En_v0), .out3(En_a0), .out4(En_a1), .out5(En_a2), .out6(En_a3), .out7(En_a4),
    .out8(En_s0), .out9(En_s1), .out10(En_s2), .out11(En_s3), .out12(En_k0), .out13(En_sp), .out14(En_fp),
    .out15(En_ra), .sel(WrREGNO), .en(WrEN));  // open: out0
  Register #(.width(32)) u_zero (.D(INPUT), .en(1'b0), .Q(zero), .clk(CLK));  // open: clr
  Register #(.width(32)) u_at (.D(INPUT), .en(En_at), .Q(at), .clk(CLK));  // open: clr
  Register #(.width(32)) u_v0 (.D(INPUT), .en(En_v0), .Q(v0), .clk(CLK));  // open: clr
  Register #(.width(32)) u_a0 (.D(INPUT), .en(En_a0), .Q(a0), .clk(CLK));  // open: clr
  Register #(.width(32)) u_a1 (.D(INPUT), .en(En_a1), .Q(a1), .clk(CLK));  // open: clr
  Register #(.width(32)) u_a2 (.D(INPUT), .en(En_a2), .Q(a2), .clk(CLK));  // open: clr
  Register #(.width(32)) u_a3 (.D(INPUT), .en(En_a3), .Q(a3), .clk(CLK));  // open: clr
  Register #(.width(32)) u_a4 (.D(INPUT), .en(En_a4), .Q(a4), .clk(CLK));  // open: clr
  Multiplexer #(.select(4), .width(32), .disabled(0), .enable("false")) multiplexer_1 (
    .in0(zero), .in1(at), .in2(v0), .in3(a0), .in4(a1), .in5(a2), .in6(a3), .in7(a4), .in8(s0), .in9(s1),
    .in10(s2), .in11(s3), .in12(k0), .in13(sp), .in14(fp), .in15(ra), .out(OUT2), .sel(RdREGNO2));
  Register #(.width(32)) u_s0 (.D(INPUT), .en(En_s0), .Q(s0), .clk(CLK));  // open: clr
  Register #(.width(32)) u_s1 (.D(INPUT), .en(En_s1), .Q(s1), .clk(CLK));  // open: clr
  Register #(.width(32)) u_s2 (.D(INPUT), .en(En_s2), .Q(s2), .clk(CLK));  // open: clr
  Register #(.width(32)) u_s3 (.D(INPUT), .en(En_s3), .Q(s3), .clk(CLK));  // open: clr
  Register #(.width(32)) u_k0 (.D(INPUT), .en(En_k0), .Q(k0), .clk(CLK));  // open: clr
  Register #(.width(32)) u_sp (.D(INPUT), .en(En_sp), .Q(sp), .clk(CLK));  // open: clr
  Register #(.width(32)) u_fp (.D(INPUT), .en(En_fp), .Q(fp), .clk(CLK));  // open: clr
  Register #(.width(32)) u_ra (.D(INPUT), .en(En_ra), .Q(ra), .clk(CLK));  // open: clr
  Multiplexer #(.select(4), .width(32), .disabled(0), .enable("false")) multiplexer_2 (
    .in0(zero), .in1(at), .in2(v0), .in3(a0), .in4(a1), .in5(a2), .in6(a3), .in7(a4), .in8(s0), .in9(s1),
    .in10(s2), .in11(s3), .in12(k0), .in13(sp), .in14(fp), .in15(ra), .out(OUT1), .sel(RdREGNO1));

  // Notes on the sheet:
  //   DO NOT MODIFY THIS FILE
endmodule

module IF_IDRR_Buffer (
  input  [31:0] PC_In,
  input  [31:0] in_2,
  input  [31:0] in_3,
  input  [31:0] in_4,
  input  [31:0] in_5,
  input  [31:0] in_6,
  input  EN,
  input  CLK,
  input  CLR,
  output [31:0] PC_Out,
  output [31:0] out_11,
  output [31:0] out_12,
  output [31:0] out_13,
  output [31:0] out_14,
  output [31:0] out_15
);

  Register #(.width(32)) register_1 (.D(PC_In), .en(EN), .Q(PC_Out), .clk(CLK), .clr(CLR));
  Register #(.width(32)) register_2 (.D(in_2), .en(EN), .Q(out_11), .clk(CLK), .clr(CLR));
  Register #(.width(32)) register_3 (.D(in_3), .en(EN), .Q(out_12), .clk(CLK), .clr(CLR));
  Register #(.width(32)) register_4 (.D(in_4), .en(EN), .Q(out_13), .clk(CLK), .clr(CLR));
  Register #(.width(32)) register_5 (.D(in_5), .en(EN), .Q(out_14), .clk(CLK), .clr(CLR));
  Register #(.width(32)) register_6 (.D(in_6), .en(EN), .Q(out_15), .clk(CLK), .clr(CLR));
endmodule

module IDRR_EX_Buffer (
  input  [31:0] PC_In,
  input  [31:0] in_2,
  input  [31:0] in_3,
  input  [31:0] in_4,
  input  [31:0] in_5,
  input  [31:0] in_6,
  input  EN,
  input  CLK,
  input  CLR,
  output [31:0] PC_Out,
  output [31:0] out_11,
  output [31:0] out_12,
  output [31:0] out_13,
  output [31:0] out_14,
  output [31:0] out_15
);

  Register #(.width(32)) register_1 (.D(PC_In), .en(EN), .Q(PC_Out), .clk(CLK), .clr(CLR));
  Register #(.width(32)) register_2 (.D(in_2), .en(EN), .Q(out_11), .clk(CLK), .clr(CLR));
  Register #(.width(32)) register_3 (.D(in_3), .en(EN), .Q(out_12), .clk(CLK), .clr(CLR));
  Register #(.width(32)) register_4 (.D(in_4), .en(EN), .Q(out_13), .clk(CLK), .clr(CLR));
  Register #(.width(32)) register_5 (.D(in_5), .en(EN), .Q(out_14), .clk(CLK), .clr(CLR));
  Register #(.width(32)) register_6 (.D(in_6), .en(EN), .Q(out_15), .clk(CLK), .clr(CLR));
endmodule

module EX_MEM_Buffer (
  input  [31:0] PC_In,
  input  [31:0] in_2,
  input  [31:0] in_3,
  input  [31:0] in_4,
  input  [31:0] in_5,
  input  [31:0] in_6,
  input  EN,
  input  CLK,
  input  CLR,
  output [31:0] PC_Out,
  output [31:0] out_11,
  output [31:0] out_12,
  output [31:0] out_13,
  output [31:0] out_14,
  output [31:0] out_15
);

  Register #(.width(32)) register_1 (.D(PC_In), .en(EN), .Q(PC_Out), .clk(CLK), .clr(CLR));
  Register #(.width(32)) register_2 (.D(in_2), .en(EN), .Q(out_11), .clk(CLK), .clr(CLR));
  Register #(.width(32)) register_3 (.D(in_3), .en(EN), .Q(out_12), .clk(CLK), .clr(CLR));
  Register #(.width(32)) register_4 (.D(in_4), .en(EN), .Q(out_13), .clk(CLK), .clr(CLR));
  Register #(.width(32)) register_5 (.D(in_5), .en(EN), .Q(out_14), .clk(CLK), .clr(CLR));
  Register #(.width(32)) register_6 (.D(in_6), .en(EN), .Q(out_15), .clk(CLK), .clr(CLR));
endmodule

module MEM_WB_Buffer (
  input  [31:0] PC_In,
  input  [31:0] in_2,
  input  [31:0] in_3,
  input  [31:0] in_4,
  input  [31:0] in_5,
  input  [31:0] in_6,
  input  EN,
  input  CLK,
  input  CLR,
  output [31:0] PC_Out,
  output [31:0] out_11,
  output [31:0] out_12,
  output [31:0] out_13,
  output [31:0] out_14,
  output [31:0] out_15
);

  Register #(.width(32)) register_1 (.D(PC_In), .en(EN), .Q(PC_Out), .clk(CLK), .clr(CLR));
  Register #(.width(32)) register_2 (.D(in_2), .en(EN), .Q(out_11), .clk(CLK), .clr(CLR));
  Register #(.width(32)) register_3 (.D(in_3), .en(EN), .Q(out_12), .clk(CLK), .clr(CLR));
  Register #(.width(32)) register_4 (.D(in_4), .en(EN), .Q(out_13), .clk(CLK), .clr(CLR));
  Register #(.width(32)) register_5 (.D(in_5), .en(EN), .Q(out_14), .clk(CLK), .clr(CLR));
  Register #(.width(32)) register_6 (.D(in_6), .en(EN), .Q(out_15), .clk(CLK), .clr(CLR));
endmodule

module ALU (
  input  [1:0] FUNC,
  input  [31:0] A,
  input  [31:0] B,
  output [31:0] OUT
);

  wire [31:0] adder_1_out, adder_2_out, nand_1_out, subtractor_1_out;

  Adder #(.width(32)) adder_1 (.a(A), .b(B), .out(adder_1_out), .cin(1'b0));  // open: cout
  assign nand_1_out = ~(A & B);  // NAND_Gate nand_1, 32 bits wide
  Subtractor #(.width(32)) subtractor_1 (.a(A), .b(B), .out(subtractor_1_out), .bin(1'b0));  // open: bout
  Adder #(.width(32)) adder_2 (.a(A), .b({32{1'b0}}), .out(adder_2_out), .cin(1'b1));  // open: cout
  Multiplexer #(.select(2), .width(32), .disabled(0), .enable("false")) multiplexer_1 (
    .in0(adder_1_out), .in1(nand_1_out), .in2(subtractor_1_out), .in3(adder_2_out), .out(OUT), .sel(FUNC));

  // Notes on the sheet:
  //   DO NOT MODIFY THIS
endmodule
