// Logisim project BOB2200-pipeline.circ as structural Verilog: 7 circuits, main circuit main
module main (
  output [1:0] LEA,
  output out_2,
  output [3:0] out_3,
  output [3:0] out_4,
  output [3:0] out_5,
  output [3:0] out_6,
  output [3:0] out_7,
  output [3:0] out_8,
  output [3:0] out_9,
  output [3:0] out_10,
  output [3:0] out_11,
  output [3:0] out_12
);

  wire ADD, ADDI, and_1_out, BNE, BNEon, brEnable, CLK, comparator_1_eq, comparator_2_eq, comparator_3_eq,
       comparator_4_eq, comparator_6_eq, comparator_7_eq, comparator_8_eq, comparator_9_eq, comparator_11_eq,
       comparator_12_eq, comparator_13_eq, comparator_15_eq, comparator_16_eq, comparator_17_eq,
       comparator_18_eq, comparator_18_lt, comparator_19_eq, equal, flush, HALT, JALR, LEA_t, LW,
       multiplexer_4_out, multiplexer_7_out, multiplexer_9_out, NAND, NOOP, not_1_out, not_2_out, not_3_out,
       not_4_out, not_5_out, or_1_out, or_2_out, or_3_out, or_4_out, or_6_out, or_7_out, or_10_out, Rx_is_0,
       Ry_is_0, Rz_is_0, SLT, stall, SW, X, Y, Z;
  wire [3:0] ex_mem_buffer_1_output_8, halt_t, mem_wb_buffer_1_output_8, multiplexer_8_out,
       multiplexer_10_out, multiplexer_11_out, Rx1, Rx2;
  wire [19:4] instruction;
  wire [27:0] ram_1_data;
  wire [31:0] adder_1_out, alu_1_output, bit_extender_2_out, BNE_PC, BR, control_sig1, control_sig2,
       control_sig3, control_sig4, Data, dual_ported_register_file_1_out1, dual_ported_register_file_1_out2,
       ex_mem_buffer_1_output, ex_mem_buffer_1_output_3, ex_mem_buffer_1_output_6, if_idrr_buffer_1_output,
       imm, instruction1, instruction2, instruction3, JALR_PC, mem_wb_buffer_1_output,
       mem_wb_buffer_1_output_2, mem_wb_buffer_1_output_3, mem_wb_buffer_1_output_6, multiplexer_1_out,
       multiplexer_2_out, multiplexer_3_out, multiplexer_5_out, multiplexer_6_out, multiplexer_12_out,
       Offset, PC, PC_stall, ram_2_data, result_mem, RX_val;

  Multiplexer #(.width(32), .disabled(0), .enable("false")) multiplexer_1 (
    .in0(multiplexer_2_out), .in1(PC_stall), .out(multiplexer_1_out), .sel(stall));
  Register #(.width(32)) u_PC (.D(multiplexer_1_out), .en(not_1_out), .Q(PC_stall), .clk(CLK));  // open: clr
  not not_1 (not_1_out, and_1_out);
  and and_1 (and_1_out, control_sig4[17], control_sig4[16], control_sig2[20], brEnable, control_sig3[18], control_sig1[24], LEA[0], LEA[1], control_sig2[26], control_sig2[25], control_sig4[23]);
  Decoder #(.select(4), .enable("false")) decoder_1 (
    .out0(ADD), .out1(NAND), .out2(ADDI), .out3(LW), .out4(SW), .out5(BNE), .out6(JALR), .out7(HALT),
    .out8(SLT), .out9(LEA_t), .out10(NOOP), .sel(out_5));  // open: out11, out12, out13, out14, out15
  and and_2 (X, not_2_out, multiplexer_4_out);
  or or_1 (or_1_out, SW, BNE);
  Comparator #(.width(4)) comparator_1 (.a(out_8), .b(out_10), .eq(comparator_1_eq));  // open: gt, lt
  Comparator #(.width(4)) comparator_2 (.a(out_8), .b(out_11), .eq(comparator_2_eq));  // open: gt, lt
  Comparator #(.width(4), .mode("unsigned")) comparator_3 (
    .a(out_8), .b(out_12), .eq(comparator_3_eq));  // open: gt, lt
  Comparator #(.width(4), .mode("unsigned")) comparator_4 (
    .a(out_4), .b(4'b0110), .eq(comparator_4_eq));  // open: gt, lt
  Multiplexer #(.width(32), .disabled(0), .enable("false")) multiplexer_2 (
    .in0(multiplexer_3_out), .in1(JALR_PC), .out(multiplexer_2_out), .sel(comparator_4_eq));
  Adder #(.width(32)) adder_1 (.a(32'h1), .b(PC_stall), .out(adder_1_out));  // open: cin, cout
  not not_2 (not_2_out, Rx_is_0);
  Comparator #(.width(4), .mode("unsigned")) comparator_5 (.a(out_8), .b(4'b0000), .eq(Rx_is_0));  // open: gt, lt
  or or_2 (or_2_out, comparator_1_eq, comparator_2_eq, comparator_3_eq);
  Multiplexer #(.width(32), .disabled(0), .enable("false")) multiplexer_3 (
    .in0(multiplexer_5_out), .in1(BNE_PC), .out(multiplexer_3_out), .sel(BNEon));
  Multiplexer #(.disabled(0), .enable("false")) multiplexer_4 (
    .in0(1'b0), .in1(or_2_out), .out(multiplexer_4_out), .sel(or_1_out));
  and and_3 (Y, not_3_out, multiplexer_7_out);
  or or_3 (or_3_out, ADD, NAND, ADDI, SW, BNE, JALR, LW, SLT);
  Comparator #(.width(4), .mode("unsigned")) comparator_6 (
    .a(out_7), .b(out_10), .eq(comparator_6_eq));  // open: gt, lt
  Comparator #(.width(4), .mode("unsigned")) comparator_7 (
    .a(out_7), .b(out_11), .eq(comparator_7_eq));  // open: gt, lt
  Comparator #(.width(4), .mode("unsigned")) comparator_8 (
    .a(out_7), .b(out_12), .eq(comparator_8_eq));  // open: gt, lt
  Comparator #(.width(4), .mode("unsigned")) comparator_9 (
    .a(halt_t), .b(4'b0111), .eq(comparator_9_eq));  // open: gt, lt
  Multiplexer #(.width(32), .disabled(0), .enable("false")) multiplexer_5 (
    .in0(multiplexer_6_out), .in1(PC_stall), .out(multiplexer_5_out), .sel(comparator_9_eq));
  Multiplexer #(.select(2), .width(32), .disabled(0), .enable("false")) multiplexer_6 (
    .in0(adder_1_out), .in1(JALR_PC), .in2(BR), .out(multiplexer_6_out),
    .sel({control_sig2[25], control_sig2[26]}));  // open: in3
  RAM #(.addrWidth(24), .dataWidth(32)) ram_1 (
    .addr(PC_stall[23:0]), .data({halt_t, ram_1_data}), .clk(1'b1));  // open: sel, ld, clr
  not not_3 (not_3_out, Ry_is_0);
  Comparator #(.width(4), .mode("unsigned")) comparator_10 (.a(out_7), .b(4'b0000), .eq(Ry_is_0));  // open: gt, lt
  or or_4 (or_4_out, comparator_6_eq, comparator_7_eq, comparator_8_eq);
  not not_4 (not_4_out, stall);
  or or_5 (stall, X, Y, Z);
  and and_4 (Z, not_5_out, multiplexer_9_out);
  or or_6 (or_6_out, ADD, NAND, SLT);
  Comparator #(.width(4), .mode("unsigned")) comparator_11 (
    .a(out_6), .b(out_10), .eq(comparator_11_eq));  // open: gt, lt
  Comparator #(.width(4), .mode("unsigned")) comparator_12 (
    .a(out_6), .b(out_11), .eq(comparator_12_eq));  // open: gt, lt
  Comparator #(.width(4), .mode("unsigned")) comparator_13 (
    .a(out_6), .b(out_12), .eq(comparator_13_eq));  // open: gt, lt
  Multiplexer #(.disabled(0), .enable("false")) multiplexer_7 (
    .in0(1'b0), .in1(or_4_out), .out(multiplexer_7_out), .sel(or_3_out));
  IF_IDRR_Buffer if_idrr_buffer_1 (
    .\input (multiplexer_6_out), .input_6({halt_t, ram_1_data}),
    .output_6({out_5, out_8, out_7, instruction, out_6}), .enable(not_4_out), .CLK(CLK),
    .\output (if_idrr_buffer_1_output), .in_9(flush));  // open: input_2, input_3, input_4, input_5, output_5, output_4, output_2, output_3
  not not_5 (not_5_out, Rz_is_0);
  Comparator #(.width(4), .mode("unsigned")) comparator_14 (.a(out_6), .b(4'b0000), .eq(Rz_is_0));  // open: gt, lt
  or or_7 (or_7_out, comparator_11_eq, comparator_12_eq, comparator_13_eq);
  Multiplexer #(.width(4), .disabled(0), .enable("false")) multiplexer_8 (
    .in0(out_6), .in1(out_8), .out(multiplexer_8_out), .sel(control_sig1[24]));
  Clock u_CLK (.out(CLK));
  Multiplexer #(.disabled(0), .enable("false")) multiplexer_9 (
    .in0(1'b0), .in1(or_7_out), .out(multiplexer_9_out), .sel(or_6_out));
  Multiplexer #(.width(4), .disabled(0), .enable("false")) multiplexer_10 (
    .in0(multiplexer_8_out), .in1(out_7), .out(multiplexer_10_out), .sel(comparator_15_eq));
  Comparator #(.width(4)) comparator_15 (.a(out_5), .b(4'b0101), .eq(comparator_15_eq));  // open: gt, lt
  assign Offset = {{12{instruction[19]}}, {instruction, out_6}};  // Bit_Extender bit_extender_1
  Multiplexer #(.width(4), .disabled(0), .enable("false")) multiplexer_11 (
    .in0(out_7), .in1(multiplexer_8_out), .out(multiplexer_11_out), .sel(comparator_15_eq));
  Dual_Ported_Register_File dual_ported_register_file_1 (
    .CLK(CLK), .WrREGNO(out_3), .RdREGNO1(multiplexer_11_out), .RdREGNO2(multiplexer_10_out), .INPUT(Data),
    .OUT1(dual_ported_register_file_1_out1), .OUT2(dual_ported_register_file_1_out2), .WrEN(control_sig4[23]));
  ROM #(.addrWidth(4), .dataWidth(32)) rom_1 (.addr(out_5), .data(control_sig1), .sel(1'b1));
  or or_8 (out_2, flush, stall);
  IDRR_EX_Buffer idrr_ex_buffer_1 (
    .\input (if_idrr_buffer_1_output), .input_2(dual_ported_register_file_1_out1),
    .input_3(dual_ported_register_file_1_out2), .input_4(Offset),
    .input_5({out_5, out_8, out_7, instruction, out_6}), .DestinationReg_2(out_8), .opcode(out_5),
    .\output (PC), .output_2(JALR_PC), .output_3(RX_val), .output_4(imm), .output_5(instruction1),
    .DestinationReg_4(out_10), .opcode_2(out_4), .enable(1'b1), .CLK(CLK), .flush1(out_2),
    .DestinationReg(out_8), .DestinationReg_3(Rx1));
  Multiplexer #(.width(32), .disabled(0), .enable("false")) multiplexer_12 (
    .in0(RX_val), .in1(imm), .out(multiplexer_12_out), .sel(control_sig2[20]));
  Comparator #(.width(4)) comparator_16 (.a(out_4), .b(4'b0110), .eq(comparator_16_eq));  // open: gt, lt
  Comparator #(.width(4)) comparator_17 (.a(out_4), .b(4'b0101), .eq(comparator_17_eq));  // open: gt, lt
  ALU alu_1 (.A(JALR_PC), .B(multiplexer_12_out), .\output (alu_1_output), .func(LEA));
  and and_5 (BNEon, comparator_17_eq, equal);
  Comparator #(.width(32)) comparator_18 (
    .a(alu_1_output), .b({32{1'b0}}), .eq(comparator_18_eq), .lt(comparator_18_lt));  // open: gt
  or or_9 (flush, comparator_16_eq, BNEon);
  Adder #(.width(32)) adder_2 (.a(PC), .b(imm), .out(BR));  // open: cin, cout
  or or_10 (or_10_out, comparator_19_eq, BNEon);
  Comparator #(.width(4)) comparator_19 (.a(out_4), .b(4'b1001), .eq(comparator_19_eq));  // open: gt, lt
  not not_6 (equal, comparator_18_eq);
  ROM #(.addrWidth(4), .dataWidth(32)) rom_2 (
    .addr(out_4),
    .data({control_sig2[31:23], LEA[0], LEA[1], control_sig2[20], brEnable, control_sig2[18:0]}), .sel(1'b1));
  Multiplexer #(.width(32), .disabled(0), .enable("false")) multiplexer_13 (
    .in0(alu_1_output), .in1(BR), .out(BNE_PC), .sel(or_10_out));
  assign bit_extender_2_out = {{31{1'b0}}, comparator_18_lt};  // Bit_Extender bit_extender_2
  EX_MEM_Buffer ex_mem_buffer_1 (
    .\input (PC), .input_2(BNE_PC), .input_3(RX_val), .input_4(instruction1), .input_6(bit_extender_2_out),
    .input_7(out_10), .input_8(out_4), .\output (ex_mem_buffer_1_output), .output_2(result_mem),
    .output_3(ex_mem_buffer_1_output_3), .output_4(instruction2), .output_6(ex_mem_buffer_1_output_6),
    .output_7(out_11), .output_8(ex_mem_buffer_1_output_8), .enable(1'b1), .CLK(CLK), .input_5(Rx1),
    .output_5(Rx2));
  ROM #(.addrWidth(4), .dataWidth(32)) rom_3 (.addr(ex_mem_buffer_1_output_8), .data(control_sig3), .sel(1'b1));
  RAM #(.addrWidth(24), .dataWidth(32), .bus("separate")) ram_2 (
    .addr(result_mem[23:0]), .din(ex_mem_buffer_1_output_3), .data(ram_2_data), .str(control_sig3[18]),
    .clk(CLK));  // open: sel, ld, clr
  MEM_WB_Buffer mem_wb_buffer_1 (
    .\input (ex_mem_buffer_1_output), .input_2(result_mem), .input_3(ram_2_data), .input_4(instruction2),
    .input_6(ex_mem_buffer_1_output_6), .input_7(out_11), .input_8(ex_mem_buffer_1_output_8),
    .\output (mem_wb_buffer_1_output), .output_2(mem_wb_buffer_1_output_2),
    .output_3(mem_wb_buffer_1_output_3), .output_4(instruction3), .output_6(mem_wb_buffer_1_output_6),
    .output_7(out_12), .output_8(mem_wb_buffer_1_output_8), .enable(1'b1), .CLK(CLK), .input_5(Rx2),
    .output_5(out_3));
  Multiplexer #(.select(2), .width(32), .disabled(0), .enable("false")) multiplexer_14 (
    .in0(mem_wb_buffer_1_output), .in1(mem_wb_buffer_1_output_2), .in2(mem_wb_buffer_1_output_3),
    .in3(mem_wb_buffer_1_output_6), .out(Data), .sel({control_sig4[16], control_sig4[17]}));
  ROM #(.addrWidth(4), .dataWidth(32)) rom_4 (.addr(mem_wb_buffer_1_output_8), .data(control_sig4), .sel(1'b1));

  assign out_9 = out_8;

  // Other names for the same wires on the sheet: RegSel = control_sig1[24];
  //   control_sig2 (some bits) = {LEA[0], LEA[1], brEnable}; immSel = control_sig2[20]; WrMEM = control_sig3[18];
  //   WrEN = control_sig4[23]; DestinationReg[3:0] = out_3; E_DstReg[3:0] = out_10; E_DstReg2[3:0] = out_11;
  //   E_DstReg3[3:0] = out_12; func[1:0] = LEA; instruction (some bits) = {out_5, out_8, out_7, out_6};
  //   Rz[3:0] = out_6; Ry[3:0] = out_7; Pre_DstReg[3:0] = out_8; Rx[3:0] = out_8; opcode_Dec[3:0] = out_5;
  //   opcode_Exc[3:0] = out_4; PCAddrSel[1:0] = {control_sig2[25], control_sig2[26]}; RY_val[31:0] = JALR_PC;
  //   WBSel[1:0] = {control_sig4[16], control_sig4[17]}

  // Notes on the sheet:
  //   Using Rx
  //   Stalling Unit
  //   Using Ry
  //   BNE
  //   Using Rz
  //   Control Sign
  //   contents of rom_1 (hex, n*v repeats v):
  //   820000 a20000 1920000 1910000 1140000 1400000 5800000 7ff0000 c30000 9a0000
  //   JALR
  //   BNE
  //   Flush
  //   contents of rom_2 (hex, n*v repeats v):
  //   820000 a20000 1920000 1910000 1140000 1400000 5800000 7ff0000 c30000 9a0000
  //   contents of rom_3 (hex, n*v repeats v):
  //   820000 a20000 1920000 1910000 1140000 1400000 5800000 7ff0000 c30000 9a0000
  //   contents of rom_4 (hex, n*v repeats v):
  //   820000 a20000 1920000 1910000 1140000 1400000 5800000 7ff0000 c30000 9a0000
endmodule

module Dual_Ported_Register_File (
  input  CLK,
  input  WrEN,
  input  [3:0] WrREGNO,
  input  [3:0] RdREGNO1,
  input  [3:0] RdREGNO2,
  input  [31:0] INPUT,
  output [31:0] OUT1,
  output [31:0] OUT2
);

  wire En_a0, En_a1, En_a2, En_at, En_fp, En_k0, En_ra, En_s0, En_s1, En_s2, En_sp, En_t0, En_t1, En_t2,
       En_v0;
  wire [31:0] a0, a1, a2, at, fp, k0, ra, s0, s1, s2, sp, t0, t1, t2, v0, zero;

  Decoder #(.select(4), .disabled(0)) decoder_1 (
    .out1(En_at), .out2(En_v0), .out3(En_a0), .out4(En_a1), .out5(En_a2), .out6(En_t0), .out7(En_t1),
    .out8(En_t2), .out9(En_s0), .out10(En_s1), .out11(En_s2), .out12(En_k0), .out13(En_sp), .out14(En_fp),
    .out15(En_ra), .sel(WrREGNO), .en(WrEN));  // open: out0
  Register #(.width(32)) u_zero (.D(INPUT), .en(1'b0), .Q(zero), .clk(CLK));  // open: clr
  Register #(.width(32)) u_at (.D(INPUT), .en(En_at), .Q(at), .clk(CLK));  // open: clr
  Register #(.width(32)) u_v0 (.D(INPUT), .en(En_v0), .Q(v0), .clk(CLK));  // open: clr
  Register #(.width(32)) u_a0 (.D(INPUT), .en(En_a0), .Q(a0), .clk(CLK));  // open: clr
  Register #(.width(32)) u_a1 (.D(INPUT), .en(En_a1), .Q(a1), .clk(CLK));  // open: clr
  Register #(.width(32)) u_a2 (.D(INPUT), .en(En_a2), .Q(a2), .clk(CLK));  // open: clr
  Register #(.width(32)) u_t0 (.D(INPUT), .en(En_t0), .Q(t0), .clk(CLK));  // open: clr
  Register #(.width(32)) u_t1 (.D(INPUT), .en(En_t1), .Q(t1), .clk(CLK));  // open: clr
  Multiplexer #(.select(4), .width(32), .disabled(0), .enable("false")) multiplexer_1 (
    .in0(zero), .in1(at), .in2(v0), .in3(a0), .in4(a1), .in5(a2), .in6(t0), .in7(t1), .in8(t2), .in9(s0),
    .in10(s1), .in11(s2), .in12(k0), .in13(sp), .in14(fp), .in15(ra), .out(OUT2), .sel(RdREGNO2));
  Register #(.width(32)) u_t2 (.D(INPUT), .en(En_t2), .Q(t2), .clk(CLK));  // open: clr
  Register #(.width(32)) u_s0 (.D(INPUT), .en(En_s0), .Q(s0), .clk(CLK));  // open: clr
  Register #(.width(32)) u_s1 (.D(INPUT), .en(En_s1), .Q(s1), .clk(CLK));  // open: clr
  Register #(.width(32)) u_s2 (.D(INPUT), .en(En_s2), .Q(s2), .clk(CLK));  // open: clr
  Register #(.width(32)) u_k0 (.D(INPUT), .en(En_k0), .Q(k0), .clk(CLK));  // open: clr
  Register #(.width(32)) u_sp (.D(INPUT), .en(En_sp), .Q(sp), .clk(CLK));  // open: clr
  Register #(.width(32)) u_fp (.D(INPUT), .en(En_fp), .Q(fp), .clk(CLK));  // open: clr
  Register #(.width(32)) u_ra (.D(INPUT), .en(En_ra), .Q(ra), .clk(CLK));  // open: clr
  Multiplexer #(.select(4), .width(32), .disabled(0), .enable("false")) multiplexer_2 (
    .in0(zero), .in1(at), .in2(v0), .in3(a0), .in4(a1), .in5(a2), .in6(t0), .in7(t1), .in8(t2), .in9(s0),
    .in10(s1), .in11(s2), .in12(k0), .in13(sp), .in14(fp), .in15(ra), .out(OUT1), .sel(RdREGNO1));
  ROM #(.addrWidth(4), .dataWidth(32)) rom_1 ();  // open: addr, data, sel

  // Notes on the sheet:
  //   MODIFY AT YOUR OWN RISK
  //   contents of rom_1 (hex, n*v repeats v):
  //   820000 a20000 920000 1910000 1140000 400000 5800000 7ff0000 c30000 9a0000
endmodule

module IF_IDRR_Buffer (
  input  [31:0] \input ,
  input  [31:0] input_2,
  input  [31:0] input_3,
  input  [31:0] input_4,
  input  [31:0] input_5,
  input  [31:0] input_6,
  input  enable,
  input  CLK,
  input  in_9,
  output [31:0] \output ,
  output [31:0] output_2,
  output [31:0] output_3,
  output [31:0] output_4,
  output [31:0] output_5,
  output [31:0] output_6
);

  wire [31:0] multiplexer_1_out, multiplexer_2_out;

  Multiplexer #(.width(32), .disabled(0), .enable("false")) multiplexer_1 (
    .in0(\input ), .in1({32{1'b0}}), .out(multiplexer_1_out), .sel(in_9));
  Register #(.width(32)) register_1 (.D(input_2), .en(enable), .Q(output_2), .clk(CLK), .clr(in_9));
  Register #(.width(32)) register_2 (.D(input_3), .en(enable), .Q(output_3), .clk(CLK), .clr(in_9));
  Register #(.width(32)) register_3 (.D(input_4), .en(enable), .Q(output_4), .clk(CLK), .clr(in_9));
  Register #(.width(32)) register_4 (.D(input_5), .en(enable), .Q(output_5), .clk(CLK), .clr(in_9));
  Multiplexer #(.width(32), .disabled(0), .enable("false")) multiplexer_2 (
    .in0(input_6), .in1({32{1'b0}}), .out(multiplexer_2_out), .sel(in_9));
  Register #(.width(32)) register_5 (.D(multiplexer_1_out), .en(enable), .Q(\output ), .clk(CLK));  // open: clr
  Register #(.width(32)) register_6 (.D(multiplexer_2_out), .en(enable), .Q(output_6), .clk(CLK));  // open: clr

  // Other names for the same wires on the sheet: Flash = in_9
endmodule

module IDRR_EX_Buffer (
  input  [31:0] \input ,
  input  [31:0] input_2,
  input  [31:0] input_3,
  input  [31:0] input_4,
  input  [31:0] input_5,
  input  [3:0] DestinationReg,
  input  [3:0] DestinationReg_2,
  input  [3:0] opcode,
  input  enable,
  input  CLK,
  input  flush1,
  output [31:0] \output ,
  output [31:0] output_2,
  output [31:0] output_3,
  output [31:0] output_4,
  output [31:0] output_5,
  output [3:0] DestinationReg_3,
  output [3:0] DestinationReg_4,
  output [3:0] opcode_2
);

  wire [3:0] multiplexer_6_out, multiplexer_7_out, multiplexer_8_out;
  wire [31:0] multiplexer_1_out, multiplexer_2_out, multiplexer_3_out, multiplexer_4_out, multiplexer_5_out;

  Register #(.width(32)) register_1 (.D(multiplexer_1_out), .en(enable), .Q(\output ), .clk(CLK));  // open: clr
  Multiplexer #(.width(32), .disabled(0), .enable("false")) multiplexer_1 (
    .in0(\input ), .in1({32{1'b0}}), .out(multiplexer_1_out), .sel(flush1));
  Multiplexer #(.width(32), .disabled(0), .enable("false")) multiplexer_2 (
    .in0(input_2), .in1({32{1'b0}}), .out(multiplexer_2_out), .sel(flush1));
  Register #(.width(32)) register_2 (.D(multiplexer_2_out), .en(enable), .Q(output_2), .clk(CLK));  // open: clr
  Register #(.width(32)) register_3 (.D(multiplexer_3_out), .en(enable), .Q(output_3), .clk(CLK));  // open: clr
  Multiplexer #(.width(32), .disabled(0), .enable("false")) multiplexer_3 (
    .in0(input_3), .in1({32{1'b0}}), .out(multiplexer_3_out), .sel(flush1));
  Register #(.width(32)) register_4 (.D(multiplexer_4_out), .en(enable), .Q(output_4), .clk(CLK));  // open: clr
  Multiplexer #(.width(32), .disabled(0), .enable("false")) multiplexer_4 (
    .in0(input_4), .in1({32{1'b0}}), .out(multiplexer_4_out), .sel(flush1));
  Multiplexer #(.width(32), .disabled(0), .enable("false")) multiplexer_5 (
    .in0(input_5), .in1({32{1'b0}}), .out(multiplexer_5_out), .sel(flush1));
  Register #(.width(32)) register_5 (.D(multiplexer_5_out), .en(enable), .Q(output_5), .clk(CLK));  // open: clr
  Register #(.width(4)) register_6 (.D(multiplexer_6_out), .en(enable), .Q(DestinationReg_3), .clk(CLK));  // open: clr
  Multiplexer #(.width(4), .disabled(0), .enable("false")) multiplexer_6 (
    .in0(DestinationReg), .in1(4'b0000), .out(multiplexer_6_out), .sel(flush1));
  Multiplexer #(.width(4), .disabled(0), .enable("false")) multiplexer_7 (
    .in0(DestinationReg_2), .in1(4'b0000), .out(multiplexer_7_out), .sel(flush1));
  Register #(.width(4)) register_7 (.D(multiplexer_7_out), .en(enable), .Q(DestinationReg_4), .clk(CLK));  // open: clr
  Multiplexer #(.width(4), .disabled(0), .enable("false")) multiplexer_8 (
    .in0(opcode), .in1(4'b1010), .out(multiplexer_8_out), .sel(flush1));
  Register #(.width(4)) register_8 (.D(multiplexer_8_out), .en(enable), .Q(opcode_2), .clk(CLK));  // open: clr

  // Other names for the same wires on the sheet: Flash = flush1
endmodule

module EX_MEM_Buffer (
  input  [31:0] \input ,
  input  [31:0] input_2,
  input  [31:0] input_3,
  input  [31:0] input_4,
  input  [3:0] input_5,
  input  [31:0] input_6,
  input  [3:0] input_7,
  input  [3:0] input_8,
  input  enable,
  input  CLK,
  output [31:0] \output ,
  output [31:0] output_2,
  output [31:0] output_3,
  output [31:0] output_4,
  output [3:0] output_5,
  output [31:0] output_6,
  output [3:0] output_7,
  output [3:0] output_8
);

  Register #(.width(32)) register_1 (.D(\input ), .en(enable), .Q(\output ), .clk(CLK));  // open: clr
  Register #(.width(32)) register_2 (.D(input_2), .en(enable), .Q(output_2), .clk(CLK));  // open: clr
  Register #(.width(32)) register_3 (.D(input_3), .en(enable), .Q(output_3), .clk(CLK));  // open: clr
  Register #(.width(32)) register_4 (.D(input_4), .en(enable), .Q(output_4), .clk(CLK));  // open: clr
  Register #(.width(4)) register_5 (.D(input_5), .en(enable), .Q(output_5), .clk(CLK));  // open: clr
  Register #(.width(32)) register_6 (.D(input_6), .en(enable), .Q(output_6), .clk(CLK));  // open: clr
  Register #(.width(4)) register_7 (.D(input_7), .en(enable), .Q(output_7), .clk(CLK));  // open: clr
  Register #(.width(4)) register_8 (.D(input_8), .en(enable), .Q(output_8), .clk(CLK));  // open: clr
endmodule

module MEM_WB_Buffer (
  input  [31:0] \input ,
  input  [31:0] input_2,
  input  [31:0] input_3,
  input  [31:0] input_4,
  input  [3:0] input_5,
  input  [31:0] input_6,
  input  [3:0] input_7,
  input  [3:0] input_8,
  input  enable,
  input  CLK,
  output [31:0] \output ,
  output [31:0] output_2,
  output [31:0] output_3,
  output [31:0] output_4,
  output [3:0] output_5,
  output [31:0] output_6,
  output [3:0] output_7,
  output [3:0] output_8
);

  Register #(.width(32)) register_1 (.D(\input ), .en(enable), .Q(\output ), .clk(CLK));  // open: clr
  Register #(.width(32)) register_2 (.D(input_2), .en(enable), .Q(output_2), .clk(CLK));  // open: clr
  Register #(.width(32)) register_3 (.D(input_3), .en(enable), .Q(output_3), .clk(CLK));  // open: clr
  Register #(.width(32)) register_4 (.D(input_4), .en(enable), .Q(output_4), .clk(CLK));  // open: clr
  Register #(.width(4)) register_5 (.D(input_5), .en(enable), .Q(output_5), .clk(CLK));  // open: clr
  Register #(.width(32)) register_6 (.D(input_6), .en(enable), .Q(output_6), .clk(CLK));  // open: clr
  Register #(.width(4)) register_7 (.D(input_7), .en(enable), .Q(output_7), .clk(CLK));  // open: clr
  Register #(.width(4)) register_8 (.D(input_8), .en(enable), .Q(output_8), .clk(CLK));  // open: clr
endmodule

module ALU (
  input  [31:0] A,
  input  [31:0] B,
  input  [1:0] func,
  output [31:0] \output 
);

  wire [31:0] adder_1_out, adder_2_out, nand_1_out, subtractor_1_out;

  Adder #(.width(32)) adder_1 (.a(A), .b(B), .out(adder_1_out), .cin(1'b0));  // open: cout
  Subtractor #(.width(32)) subtractor_1 (.a(A), .b(B), .out(subtractor_1_out), .bin(1'b0));  // open: bout
  assign nand_1_out = ~(B & A);  // NAND_Gate nand_1, 32 bits wide
  Adder #(.width(32)) adder_2 (.a(A), .b(32'h1), .out(adder_2_out), .cin(1'b0));  // open: cout
  Multiplexer #(.select(2), .width(32), .disabled(0), .enable("false")) multiplexer_1 (
    .in0(adder_1_out), .in1(subtractor_1_out), .in2(nand_1_out), .in3(adder_2_out), .out(\output ), .sel(func));
endmodule
