// Logisim project BOB2200-pipeline-EC.circ as structural Verilog: 7 circuits, main circuit main
module main (
  output [3:0] out_1
);

  wire ADD, ADDI, and_3_out, and_4_out, and_7_out, and_9_out, and_10_out, BNE, BNEon, brEnable, CLK,
       comparator_1_eq, comparator_2_eq, comparator_3_eq, comparator_4_eq, comparator_5_eq, comparator_6_eq,
       comparator_7_eq, comparator_10_eq, comparator_11_eq, comparator_12_eq, comparator_13_eq,
       comparator_15_eq, comparator_16_eq, comparator_17_eq, comparator_18_eq, comparator_19_eq,
       comparator_21_eq, comparator_21_lt, comparator_22_gt, comparator_22_lt, comparator_23_gt,
       comparator_23_lt, comparator_24_gt, comparator_24_lt, comparator_25_eq, comparator_26_eq,
       comparator_27_eq, comparator_28_eq, comparator_29_eq, comparator_30_eq, comparator_31_eq,
       comparator_32_eq, comparator_33_eq, DstReg_EX____0, DstReg_EX____reg1, DstReg_EX____reg2,
       DstReg_MEM____0, DstReg_MEM____reg1, DstReg_MEM____reg2, DstReg_WB____0, DstReg_WB____reg1,
       DstReg_WB____reg2, equal, flush, HALT, JALR, LEA, LW, multiplexer_5_out, multiplexer_8_out,
       multiplexer_15_out, NAND, NOOP, not_1_out, not_2_out, not_3_out, not_4_out, not_5_out, not_6_out,
       not_7_out, OP____LW, or_1_out, or_3_out, or_4_out, or_5_out, or_6_out, or_7_out, or_8_out, or_9_out,
       or_10_out, or_14_out, or_15_out, priority_encoder_1_gs, priority_encoder_2_gs, reg1_grouping_sel,
       reg2_grouping_sel, Rx_is_0, Ry_is_0, Rz_is_0, SLT, stall, SW, X, Y, Z;
  wire [1:0] stage_sel_no_reg1, stage_sel_no_reg2;
  wire [3:0] DestinationReg, DstReg_EX, DstReg_MEM, DstReg_WB, EBUF_output_5, halt_opcode, MBUF_output_8,
       multiplexer_6_out, opcode_Exc, opcode_mem, reg1, reg2, Rx, Rx1, Ry, Rz;
  wire [19:4] FBUF_output_6;
  wire [23:0] PC_q;
  wire [27:0] ram_1_data;
  wire [31:0] adder_1_out, adder_2_out, alu_1_output, ALU_result, compar_result, control_sig1, control_sig2,
       control_sig3, control_sig4, Data, EBUF_output, EBUF_output_2, EBUF_output_3, EBUF_output_6,
       FBUF_output, imm, Info_from_mem, instruction_ex, JALR_PC, MBUF_output, MBUF_output_2, MBUF_output_3,
       MBUF_output_6, multiplexer_1_out, multiplexer_2_out, multiplexer_3_out, multiplexer_4_out,
       multiplexer_10_out, multiplexer_11_out, multiplexer_12_out, multiplexer_16_out, multiplexer_17_out,
       Offset, out1, out1_out, out2, out2_out, PC, ram_2_data, reg2_val;
  wire [31:24] PC_q_2;

  Decoder #(.select(4), .enable("false")) decoder_1 (
    .out0(ADD), .out1(NAND), .out2(ADDI), .out3(LW), .out4(SW), .out5(BNE), .out6(JALR), .out7(HALT),
    .out8(SLT), .out9(LEA), .out10(NOOP), .sel(out_1));  // open: out11, out12, out13, out14, out15
  Comparator #(.width(4), .mode("unsigned")) comparator_1 (
    .a(opcode_Exc), .b(4'b0110), .eq(comparator_1_eq));  // open: gt, lt
  Multiplexer #(.width(32), .disabled(0), .enable("false")) multiplexer_1 (
    .in0(multiplexer_3_out), .in1(JALR_PC), .out(multiplexer_1_out), .sel(comparator_1_eq));
  Multiplexer #(.width(32), .disabled(0), .enable("false")) multiplexer_2 (
    .in0(multiplexer_1_out), .in1({PC_q_2, PC_q}), .out(multiplexer_2_out), .sel(stall));
  Register #(.width(32)) u_PC (.D(multiplexer_2_out), .en(1'b1), .Q({PC_q_2, PC_q}), .clk(CLK));  // open: clr
  Multiplexer #(.width(32), .disabled(0), .enable("false")) multiplexer_3 (
    .in0(multiplexer_4_out), .in1(ALU_result), .out(multiplexer_3_out), .sel(BNEon));
  Comparator #(.width(4), .mode("unsigned")) comparator_2 (
    .a(halt_opcode), .b(4'b0111), .eq(comparator_2_eq));  // open: gt, lt
  Multiplexer #(.width(32), .disabled(0), .enable("false")) multiplexer_4 (
    .in0(adder_1_out), .in1({PC_q_2, PC_q}), .out(multiplexer_4_out), .sel(comparator_2_eq));
  Clock u_CLK (.out(CLK));
  Comparator #(.width(4)) comparator_3 (.a(opcode_Exc), .b(4'b0110), .eq(comparator_3_eq));  // open: gt, lt
  Comparator #(.width(4)) comparator_4 (.a(opcode_Exc), .b(4'b0101), .eq(comparator_4_eq));  // open: gt, lt
  and and_1 (BNEon, comparator_4_eq, equal);
  and and_2 (X, not_1_out, multiplexer_5_out);
  or or_1 (or_1_out, SW, BNE);
  Comparator #(.width(4), .mode("unsigned")) comparator_5 (
    .a(Rx), .b(DstReg_EX), .eq(comparator_5_eq));  // open: gt, lt
  Comparator #(.width(4), .mode("unsigned")) comparator_6 (
    .a(Rx), .b(DstReg_MEM), .eq(comparator_6_eq));  // open: gt, lt
  Comparator #(.width(4), .mode("unsigned")) comparator_7 (
    .a(Rx), .b(DstReg_WB), .eq(comparator_7_eq));  // open: gt, lt
  Adder #(.width(32)) adder_1 (.a({PC_q_2, PC_q}), .b(32'h1), .out(adder_1_out));  // open: cin, cout
  RAM #(.addrWidth(24), .dataWidth(32)) ram_1 (
    .addr(PC_q), .data({halt_opcode, ram_1_data}), .clk(1'b1));  // open: sel, ld, clr
  or or_2 (flush, comparator_3_eq, BNEon);
  Comparator #(.width(4), .mode("unsigned")) comparator_8 (.a(out_1), .b(4'b0011), .eq(OP____LW));  // open: gt, lt
  and and_3 (and_3_out, OP____LW, or_3_out);
  or or_3 (or_3_out, X, Y, Z);
  and and_4 (and_4_out, reg1_grouping_sel, reg2_grouping_sel);
  not not_1 (not_1_out, Rx_is_0);
  Multiplexer #(.disabled(0), .enable("false")) multiplexer_5 (
    .in0(1'b0), .in1(or_4_out), .out(multiplexer_5_out), .sel(or_1_out));
  Comparator #(.width(4), .mode("unsigned")) comparator_9 (.a(Rx), .b(4'b0000), .eq(Rx_is_0));  // open: gt, lt
  or or_4 (or_4_out, comparator_5_eq, comparator_6_eq, comparator_7_eq);
  not not_2 (not_2_out, stall);
  and and_5 (stall, and_3_out, and_4_out);
  IF_IDRR_Buffer FBUF (
    .\input (adder_1_out), .input1({halt_opcode, ram_1_data}), .output_6({out_1, Rx, Ry, FBUF_output_6, Rz}),
    .enable(not_2_out), .CLK(CLK), .\output (FBUF_output), .in_9(flush));  // open: input_2, input_3, input_4, input_5, output_5, output_4, output_2, output_3
  and and_6 (Z, not_3_out, multiplexer_8_out);
  or or_5 (or_5_out, ADD, NAND, SLT);
  Comparator #(.width(4), .mode("unsigned")) comparator_10 (
    .a(Rz), .b(DstReg_EX), .eq(comparator_10_eq));  // open: gt, lt
  Comparator #(.width(4), .mode("unsigned")) comparator_11 (
    .a(Rz), .b(DstReg_MEM), .eq(comparator_11_eq));  // open: gt, lt
  Comparator #(.width(4), .mode("unsigned")) comparator_12 (
    .a(Rz), .b(DstReg_WB), .eq(comparator_12_eq));  // open: gt, lt
  Multiplexer #(.width(4), .disabled(0), .enable("false")) multiplexer_6 (
    .in0(Rz), .in1(Rx), .out(multiplexer_6_out), .sel(control_sig1[24]));
  not not_3 (not_3_out, Rz_is_0);
  or or_6 (or_6_out, comparator_10_eq, comparator_11_eq, comparator_12_eq);
  Dual_Ported_Register_File dual_ported_register_file_1 (
    .CLK(CLK), .WrREGNO(DestinationReg), .RdREGNO1(reg1), .RdREGNO2(reg2), .INPUT(Data), .OUT1(out1),
    .OUT2(out2), .WrEN(control_sig4[23]));
  Multiplexer #(.width(4), .disabled(0), .enable("false")) multiplexer_7 (
    .in0(multiplexer_6_out), .in1(Ry), .out(reg2), .sel(comparator_13_eq));
  Comparator #(.width(4), .mode("unsigned")) comparator_13 (
    .a(out_1), .b(4'b0101), .eq(comparator_13_eq));  // open: gt, lt
  assign Offset = {{12{FBUF_output_6[19]}}, {FBUF_output_6, Rz}};  // Bit_Extender bit_extender_1
  Multiplexer #(.disabled(0), .enable("false")) multiplexer_8 (
    .in0(1'b0), .in1(or_6_out), .out(multiplexer_8_out), .sel(or_5_out));
  Comparator #(.width(4), .mode("unsigned")) comparator_14 (.a(Rz), .b(4'b0000), .eq(Rz_is_0));  // open: gt, lt
  Multiplexer #(.width(4), .disabled(0), .enable("false")) multiplexer_9 (
    .in0(Ry), .in1(multiplexer_6_out), .out(reg1), .sel(comparator_13_eq));
  Comparator #(.width(4), .mode("unsigned")) comparator_15 (
    .a(4'b0100), .b(out_1), .eq(comparator_15_eq));  // open: gt, lt
  Comparator #(.width(4), .mode("unsigned")) comparator_16 (.a(Rx), .b(reg2), .eq(comparator_16_eq));  // open: gt, lt
  not not_4 (not_4_out, comparator_15_eq);
  and and_7 (and_7_out, not_4_out, comparator_16_eq);
  Multiplexer #(.select(2), .width(32), .disabled(0), .enable("false")) multiplexer_10 (
    .in1(Data), .in2(Info_from_mem), .in3(ALU_result), .out(multiplexer_10_out), .sel(stage_sel_no_reg1));  // open: in0
  not not_5 (not_5_out, OP____LW);
  Multiplexer #(.select(2), .width(32), .disabled(0), .enable("false")) multiplexer_11 (
    .in1(Data), .in2(Info_from_mem), .in3(ALU_result), .out(multiplexer_11_out), .sel(stage_sel_no_reg2));  // open: in0
  not not_6 (not_6_out, OP____LW);
  ROM #(.addrWidth(4), .dataWidth(32)) rom_1 (.addr(out_1), .data(control_sig1), .sel(1'b1));
  not not_7 (not_7_out, Ry_is_0);
  and and_8 (Y, not_7_out, multiplexer_15_out);
  or or_7 (or_7_out, ADD, NAND, ADDI, SW, BNE, JALR, LW, SLT);
  Comparator #(.width(4), .mode("unsigned")) comparator_17 (
    .a(Ry), .b(DstReg_EX), .eq(comparator_17_eq));  // open: gt, lt
  Comparator #(.width(4), .mode("unsigned")) comparator_18 (
    .a(Ry), .b(DstReg_MEM), .eq(comparator_18_eq));  // open: gt, lt
  or or_8 (or_8_out, comparator_17_eq, comparator_18_eq, comparator_19_eq);
  Comparator #(.width(4), .mode("unsigned")) comparator_19 (
    .a(Ry), .b(DstReg_WB), .eq(comparator_19_eq));  // open: gt, lt
  Multiplexer #(.width(32), .disabled(0), .enable("false")) multiplexer_12 (
    .in0(out2_out), .in1(out2), .out(multiplexer_12_out), .sel(and_7_out));
  Multiplexer #(.width(32), .disabled(0), .enable("false")) multiplexer_13 (
    .in0(out1), .in1(multiplexer_10_out), .out(out1_out), .sel(and_9_out));
  and and_9 (and_9_out, not_5_out, reg1_grouping_sel);
  Multiplexer #(.width(32), .disabled(0), .enable("false")) multiplexer_14 (
    .in0(out2), .in1(multiplexer_11_out), .out(out2_out), .sel(and_10_out));
  and and_10 (and_10_out, not_6_out, reg2_grouping_sel);
  Multiplexer #(.disabled(0), .enable("false")) multiplexer_15 (
    .in0(1'b0), .in1(or_8_out), .out(multiplexer_15_out), .sel(or_7_out));
  Comparator #(.width(4), .mode("unsigned")) comparator_20 (.a(Ry), .b(4'b0000), .eq(Ry_is_0));  // open: gt, lt
  or or_9 (or_9_out, stall, flush);
  IDRR_EX_Buffer DBUF (
    .\input (FBUF_output), .input_2(out1_out), .input_3(multiplexer_12_out), .input_4(Offset),
    .input_5({out_1, Rx, Ry, FBUF_output_6, Rz}), .DestinationReg_2(Rx), .opcode(out_1), .\output (PC),
    .output_2(JALR_PC), .output_3(reg2_val), .output_4(imm), .output_5(instruction_ex),
    .DestinationReg_4(DstReg_EX), .opcode_2(opcode_Exc), .enable(1'b1), .CLK(CLK), .flush1(or_9_out),
    .DestinationReg(Rx), .DestinationReg_3(Rx1));
  Multiplexer #(.width(32), .disabled(0), .enable("false")) multiplexer_16 (
    .in0(reg2_val), .in1(imm), .out(multiplexer_16_out), .sel(control_sig2[20]));
  ALU alu_1 (.A(JALR_PC), .B(multiplexer_16_out), .\output (alu_1_output), .func({control_sig2[21], control_sig2[22]}));
  Adder #(.width(32)) adder_2 (.a(PC), .b(imm), .out(adder_2_out));  // open: cin, cout
  Comparator #(.width(32)) comparator_21 (
    .a(alu_1_output), .b({32{1'b0}}), .eq(comparator_21_eq), .lt(comparator_21_lt));  // open: gt
  not not_8 (equal, comparator_21_eq);
  Comparator #(.width(4), .mode("unsigned")) comparator_22 (
    .a(DstReg_EX), .b(4'b0000), .gt(comparator_22_gt), .lt(comparator_22_lt));  // open: eq
  Comparator #(.width(4), .mode("unsigned")) comparator_23 (
    .a(DstReg_MEM), .b(4'b0000), .gt(comparator_23_gt), .lt(comparator_23_lt));  // open: eq
  Comparator #(.width(4), .mode("unsigned")) comparator_24 (
    .a(DstReg_WB), .b(4'b0000), .gt(comparator_24_gt), .lt(comparator_24_lt));  // open: eq
  Comparator #(.width(4), .mode("unsigned")) comparator_25 (
    .a(reg1), .b(DstReg_EX), .eq(comparator_25_eq));  // open: gt, lt
  Comparator #(.width(4), .mode("unsigned")) comparator_26 (
    .a(reg1), .b(DstReg_MEM), .eq(comparator_26_eq));  // open: gt, lt
  Comparator #(.width(4), .mode("unsigned")) comparator_27 (
    .a(reg1), .b(DstReg_WB), .eq(comparator_27_eq));  // open: gt, lt
  Comparator #(.width(4), .mode("unsigned")) comparator_28 (
    .a(reg2), .b(DstReg_EX), .eq(comparator_28_eq));  // open: gt, lt
  Comparator #(.width(4), .mode("unsigned")) comparator_29 (
    .a(reg2), .b(DstReg_MEM), .eq(comparator_29_eq));  // open: gt, lt
  Comparator #(.width(4), .mode("unsigned")) comparator_30 (
    .a(reg2), .b(DstReg_WB), .eq(comparator_30_eq));  // open: gt, lt
  or or_10 (or_10_out, comparator_31_eq, BNEon);
  Comparator #(.width(4), .mode("unsigned")) comparator_31 (
    .a(opcode_Exc), .b(4'b1001), .eq(comparator_31_eq));  // open: gt, lt
  ROM #(.addrWidth(4), .dataWidth(32)) rom_2 (
    .addr(opcode_Exc), .data({control_sig2[31:20], brEnable, control_sig2[18:0]}), .sel(1'b1));
  or or_11 (DstReg_EX____0, comparator_22_gt, comparator_22_lt);
  or or_12 (DstReg_MEM____0, comparator_23_gt, comparator_23_lt);
  or or_13 (DstReg_WB____0, comparator_24_gt, comparator_24_lt);
  Multiplexer #(.width(32), .disabled(0), .enable("false")) multiplexer_17 (
    .in0(alu_1_output), .in1(adder_2_out), .out(multiplexer_17_out), .sel(or_10_out));
  assign compar_result = {{31{1'b0}}, comparator_21_lt};  // Bit_Extender bit_extender_2
  Comparator #(.width(4), .mode("unsigned")) comparator_32 (
    .a(opcode_Exc), .b(4'b1000), .eq(comparator_32_eq));  // open: gt, lt
  and and_11 (DstReg_EX____reg1, comparator_25_eq, DstReg_EX____0);
  and and_12 (DstReg_MEM____reg1, comparator_26_eq, DstReg_MEM____0);
  and and_13 (DstReg_WB____reg1, comparator_27_eq, DstReg_WB____0);
  and and_14 (DstReg_EX____reg2, comparator_28_eq, DstReg_EX____0);
  and and_15 (DstReg_MEM____reg2, comparator_29_eq, DstReg_MEM____0);
  and and_16 (DstReg_WB____reg2, comparator_30_eq, DstReg_WB____0);
  Multiplexer #(.width(32), .disabled(0), .enable("false")) multiplexer_18 (
    .in0(multiplexer_17_out), .in1(compar_result), .out(ALU_result), .sel(comparator_32_eq));
  EX_MEM_Buffer EBUF (
    .\input (PC), .input_2(ALU_result), .input_3(reg2_val), .input_6(compar_result), .input_7(DstReg_EX),
    .input_8(opcode_Exc), .\output (EBUF_output), .output_2(EBUF_output_2), .output_3(EBUF_output_3),
    .output_6(EBUF_output_6), .output_7(DstReg_MEM), .output_8(opcode_mem), .enable(1'b1), .CLK(CLK),
    .input_5(Rx1), .output_5(EBUF_output_5));  // open: input_4, output_4
  Priority_Encoder #(.select(2)) priority_encoder_1 (
    .in0(1'b1), .in1(DstReg_WB____reg1), .in2(DstReg_MEM____reg1), .in3(DstReg_EX____reg1),
    .out(stage_sel_no_reg1), .gs(priority_encoder_1_gs));  // open: en_out, en_in
  or or_14 (or_14_out, DstReg_EX____reg1, DstReg_MEM____reg1, DstReg_WB____reg1);
  Priority_Encoder #(.select(2)) priority_encoder_2 (
    .in0(1'b1), .in1(DstReg_WB____reg2), .in2(DstReg_MEM____reg2), .in3(DstReg_EX____reg2),
    .out(stage_sel_no_reg2), .gs(priority_encoder_2_gs));  // open: en_out, en_in
  or or_15 (or_15_out, DstReg_EX____reg2, DstReg_MEM____reg2, DstReg_WB____reg2);
  ROM #(.addrWidth(4), .dataWidth(32)) rom_3 (.addr(opcode_mem), .data(control_sig3), .sel(1'b1));
  and and_17 (reg1_grouping_sel, priority_encoder_1_gs, or_14_out);
  and and_18 (reg2_grouping_sel, priority_encoder_2_gs, or_15_out);
  Comparator #(.width(4), .mode("unsigned")) comparator_33 (
    .a(opcode_mem), .b(4'b0011), .eq(comparator_33_eq));  // open: gt, lt
  RAM #(.addrWidth(24), .dataWidth(32), .bus("separate")) ram_2 (
    .addr(EBUF_output_2[23:0]), .din(EBUF_output_3), .data(ram_2_data), .str(control_sig3[18]), .clk(CLK));  // open: sel, ld, clr
  Multiplexer #(.width(32), .disabled(0), .enable("false")) multiplexer_19 (
    .in0(EBUF_output_2), .in1(ram_2_data), .out(Info_from_mem), .sel(comparator_33_eq));
  MEM_WB_Buffer MBUF (
    .\input (EBUF_output), .input_2(EBUF_output_2), .input_3(ram_2_data), .input_6(EBUF_output_6),
    .input_7(DstReg_MEM), .input_8(opcode_mem), .\output (MBUF_output), .output_2(MBUF_output_2),
    .output_3(MBUF_output_3), .output_6(MBUF_output_6), .output_7(DstReg_WB), .output_8(MBUF_output_8),
    .enable(1'b1), .CLK(CLK), .input_5(EBUF_output_5), .output_5(DestinationReg));  // open: input_4, output_4
  Multiplexer #(.select(2), .width(32), .disabled(0), .enable("false")) multiplexer_20 (
    .in0(MBUF_output), .in1(MBUF_output_2), .in2(MBUF_output_3), .in3(MBUF_output_6), .out(Data),
    .sel({control_sig4[16], control_sig4[17]}));
  ROM #(.addrWidth(4), .dataWidth(32)) rom_4 (.addr(MBUF_output_8), .data(control_sig4), .sel(1'b1));

  // Other names for the same wires on the sheet: opcode_Dec[3:0] = out_1; BNE_PC[31:0] = ALU_result;
  //   RegSel = control_sig1[24]; control_sig2[19] = brEnable; immSel = control_sig2[20]; WrMEM = control_sig3[18];
  //   WrEN = control_sig4[23]; E_DstReg[3:0] = DstReg_EX; E_DstReg2[3:0] = DstReg_MEM; E_DstReg3[3:0] = DstReg_WB;
  //   func[1:0] = {control_sig2[21], control_sig2[22]}; PCAddrSel[1:0] = {control_sig2[25], control_sig2[26]};
  //   reg1_val[31:0] = JALR_PC; RY_val[31:0] = JALR_PC; RX_val[31:0] = reg2_val; WB_data[31:0] = Data;
  //   WBSel[1:0] = {control_sig4[16], control_sig4[17]}

  // Notes on the sheet:
  //   IF
  //   JALR
  //   BNE
  //   Flush
  //   LW
  //   Using Rx
  //   Stalling Unit
  //   BNE
  //   Using Rz
  //   ID/RR
  //   SW
  //   contents of rom_1 (hex, n*v repeats v):
  //   820000 a20000 1920000 1910000 1140000 1400000 5800000 7ff0000 c20000 9a0000
  //   Forwarding func part
  //   Using Ry
  //   Control Sign
  //   LEA
  //   EX
  //   contents of rom_2 (hex, n*v repeats v):
  //   820000 a20000 1920000 1910000 1140000 1400000 5800000 7ff0000 c20000 9a0000
  //   SLT
  //   Data forwarding Unit
  //   From WB stage
  //   From EX stage
  //   From MEM stage
  //   MEM
  //   LW
  //   contents of rom_3 (hex, n*v repeats v):
  //   820000 a20000 1920000 1910000 1140000 1400000 5800000 7ff0000 c20000 9a0000
  //   WB
  //   contents of rom_4 (hex, n*v repeats v):
  //   820000 a20000 1920000 1910000 1140000 1400000 5800000 7ff0000 c20000 9a0000
endmodule

module Dual_Ported_Register_File (
  input  CLK,
  input  WrEN,
  input  [3:0] WrREGNO,
  input  [3:0] RdREGNO1,
  input  [3:0] RdREGNO2,
  input  [31:0] INPUT,
  output [31:0] OUT1,
  output [31:0] OUT2
);

  wire En_a0, En_a1, En_a2, En_at, En_fp, En_k0, En_ra, En_s0, En_s1, En_s2, En_sp, En_t0, En_t1, En_t2,
       En_v0;
  wire [31:0] a0, a1, a2, at, fp, k0, ra, s0, s1, s2, sp, t0, t1, t2, v0, zero;

  Decoder #(.select(4), .disabled(0)) decoder_1 (
    .out1(En_at), .out2(En_v0), .out3(En_a0), .out4(En_a1), .out5(En_a2), .out6(En_t0), .out7(En_t1),
    .out8(En_t2), .out9(En_s0), .out10(En_s1), .out11(En_s2), .out12(En_k0), .out13(En_sp), .out14(En_fp),
    .out15(En_ra), .sel(WrREGNO), .en(WrEN));  // open: out0
  Register #(.width(32)) u_zero (.D(INPUT), .en(1'b0), .Q(zero), .clk(CLK));  // open: clr
  Register #(.width(32)) u_at (.D(INPUT), .en(En_at), .Q(at), .clk(CLK));  // open: clr
  Register #(.width(32)) u_v0 (.D(INPUT), .en(En_v0), .Q(v0), .clk(CLK));  // open: clr
  Register #(.width(32)) u_a0 (.D(INPUT), .en(En_a0), .Q(a0), .clk(CLK));  // open: clr
  Register #(.width(32)) u_a1 (.D(INPUT), .en(En_a1), .Q(a1), .clk(CLK));  // open: clr
  Register #(.width(32)) u_a2 (.D(INPUT), .en(En_a2), .Q(a2), .clk(CLK));  // open: clr
  Register #(.width(32)) u_t0 (.D(INPUT), .en(En_t0), .Q(t0), .clk(CLK));  // open: clr
  Register #(.width(32)) u_t1 (.D(INPUT), .en(En_t1), .Q(t1), .clk(CLK));  // open: clr
  Multiplexer #(.select(4), .width(32), .disabled(0), .enable("false")) multiplexer_1 (
    .in0(zero), .in1(at), .in2(v0), .in3(a0), .in4(a1), .in5(a2), .in6(t0), .in7(t1), .in8(t2), .in9(s0),
    .in10(s1), .in11(s2), .in12(k0), .in13(sp), .in14(fp), .in15(ra), .out(OUT2), .sel(RdREGNO2));
  Register #(.width(32)) u_t2 (.D(INPUT), .en(En_t2), .Q(t2), .clk(CLK));  // open: clr
  Register #(.width(32)) u_s0 (.D(INPUT), .en(En_s0), .Q(s0), .clk(CLK));  // open: clr
  Register #(.width(32)) u_s1 (.D(INPUT), .en(En_s1), .Q(s1), .clk(CLK));  // open: clr
  Register #(.width(32)) u_s2 (.D(INPUT), .en(En_s2), .Q(s2), .clk(CLK));  // open: clr
  Register #(.width(32)) u_k0 (.D(INPUT), .en(En_k0), .Q(k0), .clk(CLK));  // open: clr
  Register #(.width(32)) u_sp (.D(INPUT), .en(En_sp), .Q(sp), .clk(CLK));  // open: clr
  Register #(.width(32)) u_fp (.D(INPUT), .en(En_fp), .Q(fp), .clk(CLK));  // open: clr
  Register #(.width(32)) u_ra (.D(INPUT), .en(En_ra), .Q(ra), .clk(CLK));  // open: clr
  Multiplexer #(.select(4), .width(32), .disabled(0), .enable("false")) multiplexer_2 (
    .in0(zero), .in1(at), .in2(v0), .in3(a0), .in4(a1), .in5(a2), .in6(t0), .in7(t1), .in8(t2), .in9(s0),
    .in10(s1), .in11(s2), .in12(k0), .in13(sp), .in14(fp), .in15(ra), .out(OUT1), .sel(RdREGNO1));
  ROM #(.addrWidth(4), .dataWidth(32)) rom_1 ();  // open: addr, data, sel

  // Notes on the sheet:
  //   MODIFY AT YOUR OWN RISK
  //   contents of rom_1 (hex, n*v repeats v):
  //   820000 a20000 920000 1910000 1140000 400000 5800000 7ff0000 c30000 9a0000
endmodule

module IF_IDRR_Buffer (
  input  [31:0] \input ,
  input  [31:0] input_2,
  input  [31:0] input_3,
  input  [31:0] input_4,
  input  [31:0] input_5,
  input  [31:0] input1,
  input  enable,
  input  CLK,
  input  in_9,
  output [31:0] \output ,
  output [31:0] output_2,
  output [31:0] output_3,
  output [31:0] output_4,
  output [31:0] output_5,
  output [31:0] output_6
);

  wire [31:0] multiplexer_1_out, multiplexer_2_out;

  Multiplexer #(.width(32), .disabled(0), .enable("false")) multiplexer_1 (
    .in0(\input ), .in1({32{1'b0}}), .out(multiplexer_1_out), .sel(in_9));
  Multiplexer #(.width(32), .disabled(0), .enable("false")) multiplexer_2 (
    .in0(input1), .in1({32{1'b0}}), .out(multiplexer_2_out), .sel(in_9));
  Register #(.width(32)) register_1 (.D(multiplexer_1_out), .en(enable), .Q(\output ), .clk(CLK));  // open: clr
  Register #(.width(32)) register_2 (.D(input_2), .en(enable), .Q(output_2), .clk(CLK));  // open: clr
  Register #(.width(32)) register_3 (.D(input_3), .en(enable), .Q(output_3), .clk(CLK));  // open: clr
  Register #(.width(32)) register_4 (.D(input_4), .en(enable), .Q(output_4), .clk(CLK));  // open: clr
  Register #(.width(32)) register_5 (.D(input_5), .en(enable), .Q(output_5), .clk(CLK));  // open: clr
  Register #(.width(32)) register_6 (.D(multiplexer_2_out), .en(enable), .Q(output_6), .clk(CLK));  // open: clr

  // Other names for the same wires on the sheet: Flush = in_9
endmodule

module IDRR_EX_Buffer (
  input  [31:0] \input ,
  input  [31:0] input_2,
  input  [31:0] input_3,
  input  [31:0] input_4,
  input  [31:0] input_5,
  input  [3:0] DestinationReg,
  input  [3:0] DestinationReg_2,
  input  [3:0] opcode,
  input  enable,
  input  CLK,
  input  flush1,
  output [31:0] \output ,
  output [31:0] output_2,
  output [31:0] output_3,
  output [31:0] output_4,
  output [31:0] output_5,
  output [3:0] DestinationReg_3,
  output [3:0] DestinationReg_4,
  output [3:0] opcode_2
);

  wire [3:0] multiplexer_6_out, multiplexer_7_out, multiplexer_8_out;
  wire [31:0] multiplexer_1_out, multiplexer_2_out, multiplexer_3_out, multiplexer_4_out, multiplexer_5_out;

  Register #(.width(32)) register_1 (.D(multiplexer_1_out), .en(enable), .Q(\output ), .clk(CLK));  // open: clr
  Multiplexer #(.width(32), .disabled(0), .enable("false")) multiplexer_1 (
    .in0(\input ), .in1({32{1'b0}}), .out(multiplexer_1_out), .sel(flush1));
  Register #(.width(32)) register_2 (.D(multiplexer_2_out), .en(enable), .Q(output_2), .clk(CLK));  // open: clr
  Multiplexer #(.width(32), .disabled(0), .enable("false")) multiplexer_2 (
    .in0(input_2), .in1({32{1'b0}}), .out(multiplexer_2_out), .sel(flush1));
  Multiplexer #(.width(32), .disabled(0), .enable("false")) multiplexer_3 (
    .in0(input_3), .in1({32{1'b0}}), .out(multiplexer_3_out), .sel(flush1));
  Register #(.width(32)) register_3 (.D(multiplexer_3_out), .en(enable), .Q(output_3), .clk(CLK));  // open: clr
  Multiplexer #(.width(32), .disabled(0), .enable("false")) multiplexer_4 (
    .in0(input_4), .in1({32{1'b0}}), .out(multiplexer_4_out), .sel(flush1));
  Register #(.width(32)) register_4 (.D(multiplexer_4_out), .en(enable), .Q(output_4), .clk(CLK));  // open: clr
  Multiplexer #(.width(32), .disabled(0), .enable("false")) multiplexer_5 (
    .in0(input_5), .in1({32{1'b0}}), .out(multiplexer_5_out), .sel(flush1));
  Register #(.width(32)) register_5 (.D(multiplexer_5_out), .en(enable), .Q(output_5), .clk(CLK));  // open: clr
  Multiplexer #(.width(4), .disabled(0), .enable("false")) multiplexer_6 (
    .in0(DestinationReg), .in1(4'b0000), .out(multiplexer_6_out), .sel(flush1));
  Register #(.width(4)) register_6 (.D(multiplexer_6_out), .en(enable), .Q(DestinationReg_3), .clk(CLK));  // open: clr
  Multiplexer #(.width(4), .disabled(0), .enable("false")) multiplexer_7 (
    .in0(DestinationReg_2), .in1(4'b0000), .out(multiplexer_7_out), .sel(flush1));
  Register #(.width(4)) register_7 (.D(multiplexer_7_out), .en(enable), .Q(DestinationReg_4), .clk(CLK));  // open: clr
  Register #(.width(4)) register_8 (.D(multiplexer_8_out), .en(enable), .Q(opcode_2), .clk(CLK));  // open: clr
  Multiplexer #(.width(4), .disabled(0), .enable("false")) multiplexer_8 (
    .in0(opcode), .in1(4'b1010), .out(multiplexer_8_out), .sel(flush1));

  // Other names for the same wires on the sheet: Flash = flush1
endmodule

module EX_MEM_Buffer (
  input  [31:0] \input ,
  input  [31:0] input_2,
  input  [31:0] input_3,
  input  [31:0] input_4,
  input  [3:0] input_5,
  input  [31:0] input_6,
  input  [3:0] input_7,
  input  [3:0] input_8,
  input  enable,
  input  CLK,
  output [31:0] \output ,
  output [31:0] output_2,
  output [31:0] output_3,
  output [31:0] output_4,
  output [3:0] output_5,
  output [31:0] output_6,
  output [3:0] output_7,
  output [3:0] output_8
);

  Register #(.width(32)) register_1 (.D(\input ), .en(enable), .Q(\output ), .clk(CLK));  // open: clr
  Register #(.width(32)) register_2 (.D(input_2), .en(enable), .Q(output_2), .clk(CLK));  // open: clr
  Register #(.width(32)) register_3 (.D(input_3), .en(enable), .Q(output_3), .clk(CLK));  // open: clr
  Register #(.width(32)) register_4 (.D(input_4), .en(enable), .Q(output_4), .clk(CLK));  // open: clr
  Register #(.width(4)) register_5 (.D(input_5), .en(enable), .Q(output_5), .clk(CLK));  // open: clr
  Register #(.width(32)) register_6 (.D(input_6), .en(enable), .Q(output_6), .clk(CLK));  // open: clr
  Register #(.width(4)) register_7 (.D(input_7), .en(enable), .Q(output_7), .clk(CLK));  // open: clr
  Register #(.width(4)) register_8 (.D(input_8), .en(enable), .Q(output_8), .clk(CLK));  // open: clr
endmodule

module MEM_WB_Buffer (
  input  [31:0] \input ,
  input  [31:0] input_2,
  input  [31:0] input_3,
  input  [31:0] input_4,
  input  [3:0] input_5,
  input  [31:0] input_6,
  input  [3:0] input_7,
  input  [3:0] input_8,
  input  enable,
  input  CLK,
  output [31:0] \output ,
  output [31:0] output_2,
  output [31:0] output_3,
  output [31:0] output_4,
  output [3:0] output_5,
  output [31:0] output_6,
  output [3:0] output_7,
  output [3:0] output_8
);

  Register #(.width(32)) register_1 (.D(\input ), .en(enable), .Q(\output ), .clk(CLK));  // open: clr
  Register #(.width(32)) register_2 (.D(input_2), .en(enable), .Q(output_2), .clk(CLK));  // open: clr
  Register #(.width(32)) register_3 (.D(input_3), .en(enable), .Q(output_3), .clk(CLK));  // open: clr
  Register #(.width(32)) register_4 (.D(input_4), .en(enable), .Q(output_4), .clk(CLK));  // open: clr
  Register #(.width(4)) register_5 (.D(input_5), .en(enable), .Q(output_5), .clk(CLK));  // open: clr
  Register #(.width(32)) register_6 (.D(input_6), .en(enable), .Q(output_6), .clk(CLK));  // open: clr
  Register #(.width(4)) register_7 (.D(input_7), .en(enable), .Q(output_7), .clk(CLK));  // open: clr
  Register #(.width(4)) register_8 (.D(input_8), .en(enable), .Q(output_8), .clk(CLK));  // open: clr
endmodule

module ALU (
  input  [31:0] A,
  input  [31:0] B,
  input  [1:0] func,
  output [31:0] \output 
);

  wire [31:0] adder_1_out, adder_2_out, nand_1_out, subtractor_1_out;

  Adder #(.width(32)) adder_1 (.a(A), .b(B), .out(adder_1_out), .cin(1'b0));  // open: cout
  Subtractor #(.width(32)) subtractor_1 (.a(A), .b(B), .out(subtractor_1_out), .bin(1'b0));  // open: bout
  assign nand_1_out = ~(B & A);  // NAND_Gate nand_1, 32 bits wide
  Adder #(.width(32)) adder_2 (.a(A), .b(32'h1), .out(adder_2_out), .cin(1'b0));  // open: cout
  Multiplexer #(.select(2), .width(32), .disabled(0), .enable("false")) multiplexer_1 (
    .in0(adder_1_out), .in1(subtractor_1_out), .in2(nand_1_out), .in3(adder_2_out), .out(\output ), .sel(func));
endmodule
